// Logisim project 1 bit alu.circ as structural Verilog: 1 circuit, main circuit main
module main (
  input  CIN,
  input  SUB,
  input  [2:0] op,
  input  A,
  input  B,
  input  LESS,
  output RES,
  output COUT,
  output SET
);

  wire and_1_out, nor_1_out, or_1_out, xor_1_out, xor_2_out;

  xor xor_1 (xor_1_out, SUB, B);
  and and_1 (and_1_out, A, B);
  or or_1 (or_1_out, A, B);
  xor xor_2 (xor_2_out, A, B);
  nor nor_1 (nor_1_out, A, B);
  Adder #(.width(1)) adder_1 (.a(A), .b(xor_1_out), .out(SET), .cin(CIN), .cout(COUT));
  Multiplexer #(.select(3)) multiplexer_1 (
    .in0(and_1_out), .in1(or_1_out), .in2(xor_2_out), .in3(nor_1_out), .in4(SET), .in5(LESS), .out(RES),
    .sel(op));  // open: in6, in7, en
endmodule
