// Logisim project ALU.circ as structural Verilog: 1 circuit, main circuit main
module main (
  input  sub,
  input  [2:0] op,
  input  [31:0] in_3,
  input  [31:0] in_4,
  output [31:0] out_5
);

  wire main_1_cout, main_2_cout, main_3_cout, main_4_cout, main_5_cout, main_6_cout, main_7_cout,
       main_8_cout, main_9_cout, main_10_cout, main_11_cout, main_12_cout, main_13_cout, main_14_cout,
       main_15_cout, main_16_cout, main_17_cout, main_18_cout, main_19_cout, main_20_cout, main_21_cout,
       main_22_cout, main_23_cout, main_24_cout, main_25_cout, main_26_cout, main_27_cout, main_28_cout,
       main_29_cout, main_30_cout, main_31_cout, main_32_set;

  _1_bit_alu_main main_1 (
    .A(in_3[0]), .op(op), .B(in_4[0]), .LESS(main_32_set), .RES(out_5[0]), .SUB(sub), .CIN(sub),
    .COUT(main_1_cout));  // open: SET
  _1_bit_alu_main main_2 (
    .A(in_3[1]), .op(op), .B(in_4[1]), .LESS(1'b0), .RES(out_5[1]), .SUB(sub), .CIN(main_1_cout),
    .COUT(main_2_cout));  // open: SET
  _1_bit_alu_main main_3 (
    .A(in_3[2]), .op(op), .B(in_4[2]), .LESS(1'b0), .RES(out_5[2]), .SUB(sub), .CIN(main_2_cout),
    .COUT(main_3_cout));  // open: SET
  _1_bit_alu_main main_4 (
    .A(in_3[3]), .op(op), .B(in_4[3]), .LESS(1'b0), .RES(out_5[3]), .SUB(sub), .CIN(main_3_cout),
    .COUT(main_4_cout));  // open: SET
  _1_bit_alu_main main_5 (
    .A(in_3[4]), .op(op), .B(in_4[4]), .LESS(1'b0), .RES(out_5[4]), .SUB(sub), .CIN(main_4_cout),
    .COUT(main_5_cout));  // open: SET
  _1_bit_alu_main main_6 (
    .A(in_3[5]), .op(op), .B(in_4[5]), .LESS(1'b0), .RES(out_5[5]), .SUB(sub), .CIN(main_5_cout),
    .COUT(main_6_cout));  // open: SET
  _1_bit_alu_main main_7 (
    .A(in_3[6]), .op(op), .B(in_4[6]), .LESS(1'b0), .RES(out_5[6]), .SUB(sub), .CIN(main_6_cout),
    .COUT(main_7_cout));  // open: SET
  _1_bit_alu_main main_8 (
    .A(in_3[7]), .op(op), .B(in_4[7]), .LESS(1'b0), .RES(out_5[7]), .SUB(sub), .CIN(main_7_cout),
    .COUT(main_8_cout));  // open: SET
  _1_bit_alu_main main_9 (
    .A(in_3[8]), .op(op), .B(in_4[8]), .LESS(1'b0), .RES(out_5[8]), .SUB(sub), .CIN(main_8_cout),
    .COUT(main_9_cout));  // open: SET
  _1_bit_alu_main main_10 (
    .A(in_3[9]), .op(op), .B(in_4[9]), .LESS(1'b0), .RES(out_5[9]), .SUB(sub), .CIN(main_9_cout),
    .COUT(main_10_cout));  // open: SET
  _1_bit_alu_main main_11 (
    .A(in_3[10]), .op(op), .B(in_4[10]), .LESS(1'b0), .RES(out_5[10]), .SUB(sub), .CIN(main_10_cout),
    .COUT(main_11_cout));  // open: SET
  _1_bit_alu_main main_12 (
    .A(in_3[11]), .op(op), .B(in_4[11]), .LESS(1'b0), .RES(out_5[11]), .SUB(sub), .CIN(main_11_cout),
    .COUT(main_12_cout));  // open: SET
  _1_bit_alu_main main_13 (
    .A(in_3[12]), .op(op), .B(in_4[12]), .LESS(1'b0), .RES(out_5[12]), .SUB(sub), .CIN(main_12_cout),
    .COUT(main_13_cout));  // open: SET
  _1_bit_alu_main main_14 (
    .A(in_3[13]), .op(op), .B(in_4[13]), .LESS(1'b0), .RES(out_5[13]), .SUB(sub), .CIN(main_13_cout),
    .COUT(main_14_cout));  // open: SET
  _1_bit_alu_main main_15 (
    .A(in_3[14]), .op(op), .B(in_4[14]), .LESS(1'b0), .RES(out_5[14]), .SUB(sub), .CIN(main_14_cout),
    .COUT(main_15_cout));  // open: SET
  _1_bit_alu_main main_16 (
    .A(in_3[15]), .op(op), .B(in_4[15]), .LESS(1'b0), .RES(out_5[15]), .SUB(sub), .CIN(main_15_cout),
    .COUT(main_16_cout));  // open: SET
  _1_bit_alu_main main_17 (
    .A(in_3[16]), .op(op), .B(in_4[16]), .LESS(1'b0), .RES(out_5[16]), .SUB(sub), .CIN(main_16_cout),
    .COUT(main_17_cout));  // open: SET
  _1_bit_alu_main main_18 (
    .A(in_3[17]), .op(op), .B(in_4[17]), .LESS(1'b0), .RES(out_5[17]), .SUB(sub), .CIN(main_17_cout),
    .COUT(main_18_cout));  // open: SET
  _1_bit_alu_main main_19 (
    .A(in_3[18]), .op(op), .B(in_4[18]), .LESS(1'b0), .RES(out_5[18]), .SUB(sub), .CIN(main_18_cout),
    .COUT(main_19_cout));  // open: SET
  _1_bit_alu_main main_20 (
    .A(in_3[19]), .op(op), .B(in_4[19]), .LESS(1'b0), .RES(out_5[19]), .SUB(sub), .CIN(main_19_cout),
    .COUT(main_20_cout));  // open: SET
  _1_bit_alu_main main_21 (
    .A(in_3[20]), .op(op), .B(in_4[20]), .LESS(1'b0), .RES(out_5[20]), .SUB(sub), .CIN(main_20_cout),
    .COUT(main_21_cout));  // open: SET
  _1_bit_alu_main main_22 (
    .A(in_3[21]), .op(op), .B(in_4[21]), .LESS(1'b0), .RES(out_5[21]), .SUB(sub), .CIN(main_21_cout),
    .COUT(main_22_cout));  // open: SET
  _1_bit_alu_main main_23 (
    .A(in_3[22]), .op(op), .B(in_4[22]), .LESS(1'b0), .RES(out_5[22]), .SUB(sub), .CIN(main_22_cout),
    .COUT(main_23_cout));  // open: SET
  _1_bit_alu_main main_24 (
    .A(in_3[23]), .op(op), .B(in_4[23]), .LESS(1'b0), .RES(out_5[23]), .SUB(sub), .CIN(main_23_cout),
    .COUT(main_24_cout));  // open: SET
  _1_bit_alu_main main_25 (
    .A(in_3[24]), .op(op), .B(in_4[24]), .LESS(1'b0), .RES(out_5[24]), .SUB(sub), .CIN(main_24_cout),
    .COUT(main_25_cout));  // open: SET
  _1_bit_alu_main main_26 (
    .A(in_3[25]), .op(op), .B(in_4[25]), .LESS(1'b0), .RES(out_5[25]), .SUB(sub), .CIN(main_25_cout),
    .COUT(main_26_cout));  // open: SET
  _1_bit_alu_main main_27 (
    .A(in_3[26]), .op(op), .B(in_4[26]), .LESS(1'b0), .RES(out_5[26]), .SUB(sub), .CIN(main_26_cout),
    .COUT(main_27_cout));  // open: SET
  _1_bit_alu_main main_28 (
    .A(in_3[27]), .op(op), .B(in_4[27]), .LESS(1'b0), .RES(out_5[27]), .SUB(sub), .CIN(main_27_cout),
    .COUT(main_28_cout));  // open: SET
  _1_bit_alu_main main_29 (
    .A(in_3[28]), .op(op), .B(in_4[28]), .LESS(1'b0), .RES(out_5[28]), .SUB(sub), .CIN(main_28_cout),
    .COUT(main_29_cout));  // open: SET
  _1_bit_alu_main main_30 (
    .A(in_3[29]), .op(op), .B(in_4[29]), .LESS(1'b0), .RES(out_5[29]), .SUB(sub), .CIN(main_29_cout),
    .COUT(main_30_cout));  // open: SET
  _1_bit_alu_main main_31 (
    .A(in_3[30]), .op(op), .B(in_4[30]), .LESS(1'b0), .RES(out_5[30]), .SUB(sub), .CIN(main_30_cout),
    .COUT(main_31_cout));  // open: SET
  _1_bit_alu_main main_32 (
    .A(in_3[31]), .op(op), .B(in_4[31]), .LESS(1'b0), .RES(out_5[31]), .SET(main_32_set), .SUB(sub),
    .CIN(main_31_cout));  // open: COUT
endmodule
