// Logisim project ALU.circ as structural Verilog: 1 circuit, main circuit main
module main (
  input  [31:0] RS1,
  input  [31:0] IMM,
  input  [31:0] RS2,
  input  [7:0] PC,
  input  [31:0] inst_1_32,
  input  [4:0] inst_33_37,
  input  ALU_en,
  output [7:0] Dmem_address,
  output [7:0] PC_WR,
  output [31:0] ALU__out
);

  wire adder_4_cout, adder_5_cout, and_3_out, not_3_out, not_4_out, or_2_out, or_3_out, or_4_out, or_5_out,
       or_7_out, xor_4_out, xor_5_out, xor_6_out, xor_7_out;
  wire [4:0] bit_extender_5_out, bit_extender_9_out, bit_extender_10_out, bit_extender_11_out,
       bit_extender_14_out, bit_extender_15_out;
  wire [7:0] bit_extender_25_out;
  wire [11:0] adder_2_out, adder_3_out, adder_4_out, and_1_out, bit_extender_2_out, bit_extender_3_out,
       bit_extender_4_out, bit_extender_12_out, bit_extender_13_out, bit_extender_19_out,
       bit_extender_21_out, bit_extender_22_out, controlled_buffer_13_out, controlled_buffer_19_out,
       controlled_buffer_20_out, not_1_out, ORI_out, pull_resistor_2_node, pull_resistor_3_node,
       pull_resistor_4_node, pull_resistor_13_node, xor_1_out;
  wire [19:0] adder_6_out, bit_extender_20_out;
  wire [31:0] ADD, adder_1_out, adder_5_out, ADDI, AND, and_2_out, ANDI, bit_extender_16_out,
       bit_extender_23_out, bit_extender_24_out, controlled_buffer_16_out, controlled_buffer_17_out,
       not_2_out, OR, or_1_out, or_6_out, ORI, PC_t, shifter_1_out, shifter_2_out, shifter_3_out,
       shifter_4_out, shifter_5_out, shifter_6_out, SLL, SLLI, SLT, SLTI, SLTU, SLTUI, SRA, SRAI, SRL, SRLI,
       XOR, xor_2_out, xor_3_out, XORI;

  Pull_Resistor pull_resistor_1 (.node(inst_1_32));
  assign PC_t = {{24{1'b0}}, PC};  // Bit_Extender bit_extender_1
  Bit_Extender #(.in_width(32), .out_width(12)) bit_extender_2 (.in(RS1), .out(bit_extender_2_out));
  Bit_Extender #(.in_width(32), .out_width(12)) bit_extender_3 (.in(RS1), .out(bit_extender_3_out));
  Bit_Extender #(.in_width(32), .out_width(12)) bit_extender_4 (.in(RS1), .out(bit_extender_4_out));
  Bit_Extender #(.in_width(12), .out_width(5)) bit_extender_5 (.in(IMM[11:0]), .out(bit_extender_5_out));
  Pull_Resistor pull_resistor_2 (.node(pull_resistor_2_node));
  assign pull_resistor_2_node = inst_1_32[14] ? xor_1_out : 12'bz;  // Controlled_Buffer controlled_buffer_1
  assign xor_1_out = bit_extender_2_out ^ IMM[11:0];  // XOR_Gate xor_1, 12 bits wide
  Pull_Resistor pull_resistor_3 (.node(pull_resistor_3_node));
  assign ORI_out = bit_extender_3_out | IMM[11:0];  // OR_Gate ORI, 12 bits wide
  assign pull_resistor_3_node = inst_1_32[15] ? ORI_out : 12'bz;  // Controlled_Buffer controlled_buffer_2
  Pull_Resistor pull_resistor_4 (.node(pull_resistor_4_node));
  assign and_1_out = bit_extender_4_out & IMM[11:0];  // AND_Gate and_1, 12 bits wide
  assign pull_resistor_4_node = inst_1_32[16] ? and_1_out : 12'bz;  // Controlled_Buffer controlled_buffer_3
  assign SLLI = inst_1_32[17] ? shifter_1_out : 32'bz;  // Controlled_Buffer controlled_buffer_4
  Shifter #(.width(32)) shifter_1 (.in(RS1), .\dist (bit_extender_5_out), .out(shifter_1_out));
  Pull_Resistor pull_resistor_5 (.node(SLLI));
  assign XORI = {{20{1'b0}}, pull_resistor_2_node};  // Bit_Extender bit_extender_6
  assign ORI = {{20{1'b0}}, pull_resistor_3_node};  // Bit_Extender bit_extender_7
  assign ANDI = {{20{1'b0}}, pull_resistor_4_node};  // Bit_Extender bit_extender_8
  Bit_Extender #(.in_width(12), .out_width(5)) bit_extender_9 (.in(IMM[11:0]), .out(bit_extender_9_out));
  Bit_Extender #(.in_width(12), .out_width(5)) bit_extender_10 (.in(IMM[11:0]), .out(bit_extender_10_out));
  Bit_Extender #(.in_width(32), .out_width(5)) bit_extender_11 (.in(RS2), .out(bit_extender_11_out));
  assign xor_2_out = RS1 ^ RS2;  // XOR_Gate xor_2, 32 bits wide
  Shifter #(.width(32), .shift("lr")) shifter_2 (.in(RS1), .\dist (bit_extender_9_out), .out(shifter_2_out));
  Shifter #(.width(32), .shift("ar")) shifter_3 (.in(RS1), .\dist (bit_extender_10_out), .out(shifter_3_out));
  assign SRAI = inst_1_32[19] ? shifter_3_out : 32'bz;  // Controlled_Buffer controlled_buffer_5
  Pull_Resistor pull_resistor_6 (.node(SRAI));
  Pull_Resistor pull_resistor_7 (.node(SLL));
  Shifter #(.width(32)) shifter_4 (.in(RS1), .\dist (bit_extender_11_out), .out(shifter_4_out));
  assign SLL = inst_1_32[2] ? shifter_4_out : 32'bz;  // Controlled_Buffer controlled_buffer_6
  assign XOR = inst_1_32[5] ? xor_2_out : 32'bz;  // Controlled_Buffer controlled_buffer_7
  Pull_Resistor pull_resistor_8 (.node(XOR));
  assign SRLI = inst_1_32[18] ? shifter_2_out : 32'bz;  // Controlled_Buffer controlled_buffer_8
  Pull_Resistor pull_resistor_9 (.node(SRLI));
  Bit_Extender #(.in_width(32), .out_width(12)) bit_extender_12 (.in(RS1), .out(bit_extender_12_out));
  Bit_Extender #(.in_width(32), .out_width(12)) bit_extender_13 (.in(RS1), .out(bit_extender_13_out));
  Bit_Extender #(.in_width(32), .out_width(5)) bit_extender_14 (.in(RS2), .out(bit_extender_14_out));
  Bit_Extender #(.in_width(32), .out_width(5)) bit_extender_15 (.in(RS2), .out(bit_extender_15_out));
  assign bit_extender_16_out = {{31{inst_1_32[1]}}, inst_1_32[1]};  // Bit_Extender bit_extender_16
  Shifter #(.width(32), .shift("lr")) shifter_5 (.in(RS1), .\dist (bit_extender_14_out), .out(shifter_5_out));
  assign SRA = inst_1_32[7] ? shifter_6_out : 32'bz;  // Controlled_Buffer controlled_buffer_9
  Pull_Resistor pull_resistor_10 (.node(SRA));
  Shifter #(.width(32), .shift("ar")) shifter_6 (.in(RS1), .\dist (bit_extender_15_out), .out(shifter_6_out));
  Pull_Resistor pull_resistor_11 (.node(OR));
  assign or_1_out = RS1 | RS2;  // OR_Gate or_1, 32 bits wide
  assign OR = inst_1_32[8] ? or_1_out : 32'bz;  // Controlled_Buffer controlled_buffer_10
  assign AND = inst_1_32[9] ? and_2_out : 32'bz;  // Controlled_Buffer controlled_buffer_11
  Pull_Resistor pull_resistor_12 (.node(AND));
  assign and_2_out = RS1 & RS2;  // AND_Gate and_2, 32 bits wide
  Adder #(.width(32)) adder_1 (.a(RS1), .b(xor_3_out), .out(adder_1_out), .cin(inst_1_32[1]));  // open: cout
  assign xor_3_out = RS2 ^ bit_extender_16_out;  // XOR_Gate xor_3, 32 bits wide
  Pull_Resistor pull_resistor_13 (.node(pull_resistor_13_node));
  Adder #(.width(12)) adder_2 (.a(bit_extender_12_out), .b(IMM[11:0]), .out(adder_2_out), .cin(1'b0));  // open: cout
  assign pull_resistor_13_node = inst_1_32[10] ? adder_2_out : 12'bz;  // Controlled_Buffer controlled_buffer_12
  assign controlled_buffer_13_out = or_2_out ? adder_3_out : 12'bz;  // Controlled_Buffer controlled_buffer_13
  Pull_Resistor pull_resistor_14 (.node(controlled_buffer_13_out));
  Adder #(.width(12)) adder_3 (.a(bit_extender_13_out), .b(IMM[11:0]), .out(adder_3_out), .cin(1'b0));  // open: cout
  or or_2 (or_2_out, inst_1_32[21], inst_1_32[22], inst_1_32[20], inst_33_37[1], inst_33_37[4], inst_33_37[0], inst_33_37[2], inst_33_37[3]);
  assign SRL = inst_1_32[6] ? shifter_5_out : 32'bz;  // Controlled_Buffer controlled_buffer_14
  Pull_Resistor pull_resistor_15 (.node(SRL));
  Pull_Resistor pull_resistor_16 (.node(ADD));
  assign ADD = or_3_out ? adder_1_out : 32'bz;  // Controlled_Buffer controlled_buffer_15
  or or_3 (or_3_out, inst_1_32[1], inst_1_32[0]);
  assign ADDI = {{20{1'b0}}, pull_resistor_13_node};  // Bit_Extender bit_extender_17
  Bit_Extender #(.in_width(12), .out_width(8)) bit_extender_18 (.in(controlled_buffer_13_out), .out(Dmem_address));
  or or_4 (or_4_out, inst_1_32[25], inst_1_32[11]);
  assign controlled_buffer_16_out = or_4_out ? PC_t : 32'bz;  // Controlled_Buffer controlled_buffer_16
  Pull_Resistor pull_resistor_17 (.node(controlled_buffer_16_out));
  assign controlled_buffer_17_out = or_5_out ? RS2 : 32'bz;  // Controlled_Buffer controlled_buffer_17
  Pull_Resistor pull_resistor_18 (.node(controlled_buffer_17_out));
  or or_5 (or_5_out, inst_1_32[20], inst_1_32[21], inst_1_32[22]);
  Bit_Extender #(.in_width(32), .out_width(12)) bit_extender_19 (.in(RS1), .out(bit_extender_19_out));
  assign not_1_out = ~IMM[11:0];  // NOT_Gate not_1, 12 bits wide
  assign not_2_out = ~RS2;  // NOT_Gate not_2, 32 bits wide
  assign ALU__out = and_3_out ? or_6_out : 32'bz;  // Controlled_Buffer controlled_buffer_18
  Pull_Resistor pull_resistor_19 (.node(ALU__out));
  assign or_6_out = controlled_buffer_16_out | XORI | ORI | ANDI | SLLI | SRLI | SRAI | SLL | XOR | SRL | SRA | OR | AND | ADD | ADDI | SLTI | SLTUI | SLT | SLTU | controlled_buffer_17_out;  // OR_Gate or_6, 32 bits wide
  and and_3 (and_3_out, ALU_en, xor_4_out);
  Adder #(.width(12)) adder_4 (
    .a(bit_extender_19_out), .b(not_1_out), .out(adder_4_out), .cin(1'b1), .cout(adder_4_cout));
  Adder #(.width(32)) adder_5 (.a(RS1), .b(not_2_out), .out(adder_5_out), .cin(1'b1), .cout(adder_5_cout));
  Bit_Extender #(.in_width(32), .out_width(20)) bit_extender_20 (.in(PC_t), .out(bit_extender_20_out));
  ExactlyOne xor_4 (
    .out(xor_4_out), .in0(xor_5_out), .in1(inst_33_37[1]), .in2(inst_33_37[0]), .in3(inst_33_37[3]),
    .in4(inst_33_37[2]), .in5(inst_33_37[4]));
  not not_3 (not_3_out, adder_4_cout);
  not not_4 (not_4_out, adder_5_cout);
  ExactlyOne xor_5 (
    .out(xor_5_out), .in0(inst_1_32[0]), .in1(inst_1_32[1]), .in2(inst_1_32[2]), .in3(inst_1_32[3]),
    .in4(inst_1_32[4]), .in5(inst_1_32[5]), .in6(inst_1_32[6]), .in7(inst_1_32[7]), .in8(inst_1_32[8]),
    .in9(inst_1_32[9]), .in10(inst_1_32[10]), .in11(inst_1_32[11]), .in12(inst_1_32[12]),
    .in13(inst_1_32[13]), .in14(inst_1_32[14]), .in15(inst_1_32[15]), .in16(inst_1_32[16]),
    .in17(inst_1_32[17]), .in18(inst_1_32[18]), .in19(inst_1_32[19]), .in20(inst_1_32[20]),
    .in21(inst_1_32[21]), .in22(inst_1_32[22]), .in23(inst_1_32[23]), .in24(inst_1_32[24]),
    .in25(inst_1_32[25]), .in26(inst_1_32[26]), .in27(inst_1_32[27]), .in28(inst_1_32[28]),
    .in29(inst_1_32[29]), .in30(inst_1_32[30]), .in31(inst_1_32[31]));
  assign bit_extender_21_out = {{11{1'b0}}, xor_6_out};  // Bit_Extender bit_extender_21
  xor xor_6 (xor_6_out, IMM[11], adder_4_out[11]);
  assign bit_extender_22_out = {{11{1'b0}}, not_3_out};  // Bit_Extender bit_extender_22
  xor xor_7 (xor_7_out, RS2[31], adder_5_out[31]);
  assign bit_extender_23_out = {{31{1'b0}}, xor_7_out};  // Bit_Extender bit_extender_23
  assign bit_extender_24_out = {{31{1'b0}}, not_4_out};  // Bit_Extender bit_extender_24
  Adder #(.width(20)) adder_6 (.a(bit_extender_20_out), .b(IMM[20:1]), .out(adder_6_out), .cin(1'b0));  // open: cout
  Bit_Extender #(.in_width(20), .out_width(8)) bit_extender_25 (.in(adder_6_out), .out(bit_extender_25_out));
  or or_7 (or_7_out, inst_1_32[25], inst_1_32[11]);
  assign controlled_buffer_19_out = inst_1_32[12] ? bit_extender_21_out : 12'bz;  // Controlled_Buffer controlled_buffer_19
  Pull_Resistor pull_resistor_20 (.node(controlled_buffer_19_out));
  assign controlled_buffer_20_out = inst_1_32[13] ? bit_extender_22_out : 12'bz;  // Controlled_Buffer controlled_buffer_20
  Pull_Resistor pull_resistor_21 (.node(controlled_buffer_20_out));
  Pull_Resistor pull_resistor_22 (.node(SLT));
  assign SLT = inst_1_32[3] ? bit_extender_23_out : 32'bz;  // Controlled_Buffer controlled_buffer_21
  assign SLTU = inst_1_32[4] ? bit_extender_24_out : 32'bz;  // Controlled_Buffer controlled_buffer_22
  Pull_Resistor pull_resistor_23 (.node(SLTU));
  assign PC_WR = or_7_out ? bit_extender_25_out : 8'bz;  // Controlled_Buffer controlled_buffer_23
  Pull_Resistor pull_resistor_24 (.node(PC_WR));
  assign SLTI = {{20{1'b0}}, controlled_buffer_19_out};  // Bit_Extender bit_extender_26
  assign SLTUI = {{20{1'b0}}, controlled_buffer_20_out};  // Bit_Extender bit_extender_27

  // Other names for the same wires on the sheet: IMM_0_11[11:0] = IMM[11:0]; IMM_1_12[11:0] = IMM[12:1];
  //   IMM_1_20[19:0] = IMM[20:1]; IMM_12_31[19:0] = IMM[31:12]; add_t = inst_1_32[0]; sub = inst_1_32[1];
  //   sll_t = inst_1_32[2]; slt_t = inst_1_32[3]; sltu_t = inst_1_32[4]; xor_t = inst_1_32[5]; srl_t = inst_1_32[6];
  //   sra_t = inst_1_32[7]; or_t = inst_1_32[8]; and_t = inst_1_32[9]; addi_t = inst_1_32[10]; jalr = inst_1_32[11];
  //   slti_t = inst_1_32[12]; sltui_t = inst_1_32[13]; xori_t = inst_1_32[14]; ori_t = inst_1_32[15];
  //   andi_t = inst_1_32[16]; slli_t = inst_1_32[17]; srli_t = inst_1_32[18]; srai_t = inst_1_32[19];
  //   sb = inst_1_32[20]; sh = inst_1_32[21]; sw = inst_1_32[22]; lui = inst_1_32[23]; auipc = inst_1_32[24];
  //   jal = inst_1_32[25]; beq = inst_1_32[26]; bne = inst_1_32[27]; blt = inst_1_32[28]; bge = inst_1_32[29];
  //   bltu = inst_1_32[30]; bgeu = inst_1_32[31]; lb = inst_33_37[0]; lh = inst_33_37[1]; lw = inst_33_37[2];
  //   lbu = inst_33_37[3]; lhu = inst_33_37[4]; op1[31:0] = RS1; op2[31:0] = RS2
endmodule
