// Logisim project 32-bit register.circ as structural Verilog: 2 circuits, main circuit 32-bit register
module _32_bit_register (
  input  Ld,
  input  Clr,
  input  Str,
  input  [31:0] _32_bit_input,
  output [31:0] _32_bit_output
);

  wire CLK_out, pull_resistor_1_node;
  wire [31:0] d_flip_flop_1_q;

  Clock CLK (.out(CLK_out));
  Pull_Resistor pull_resistor_1 (.node(pull_resistor_1_node));
  assign pull_resistor_1_node = Str ? CLK_out : 1'bz;  // Controlled_Buffer controlled_buffer_1
  D_flip_flop d_flip_flop_1 (
    .D(_32_bit_input[0]), .CLK(pull_resistor_1_node), .Clr(Clr), .Q(d_flip_flop_1_q[0]));  // open: nQ
  D_flip_flop d_flip_flop_2 (
    .D(_32_bit_input[1]), .CLK(pull_resistor_1_node), .Clr(Clr), .Q(d_flip_flop_1_q[1]));  // open: nQ
  D_flip_flop d_flip_flop_3 (
    .D(_32_bit_input[2]), .CLK(pull_resistor_1_node), .Clr(Clr), .Q(d_flip_flop_1_q[2]));  // open: nQ
  D_flip_flop d_flip_flop_4 (
    .D(_32_bit_input[3]), .CLK(pull_resistor_1_node), .Clr(Clr), .Q(d_flip_flop_1_q[3]));  // open: nQ
  D_flip_flop d_flip_flop_5 (
    .D(_32_bit_input[4]), .CLK(pull_resistor_1_node), .Clr(Clr), .Q(d_flip_flop_1_q[4]));  // open: nQ
  D_flip_flop d_flip_flop_6 (
    .D(_32_bit_input[5]), .CLK(pull_resistor_1_node), .Clr(Clr), .Q(d_flip_flop_1_q[5]));  // open: nQ
  D_flip_flop d_flip_flop_7 (
    .D(_32_bit_input[6]), .CLK(pull_resistor_1_node), .Clr(Clr), .Q(d_flip_flop_1_q[6]));  // open: nQ
  D_flip_flop d_flip_flop_8 (
    .D(_32_bit_input[7]), .CLK(pull_resistor_1_node), .Clr(Clr), .Q(d_flip_flop_1_q[7]));  // open: nQ
  D_flip_flop d_flip_flop_9 (
    .D(_32_bit_input[8]), .CLK(pull_resistor_1_node), .Clr(Clr), .Q(d_flip_flop_1_q[8]));  // open: nQ
  D_flip_flop d_flip_flop_10 (
    .D(_32_bit_input[9]), .CLK(pull_resistor_1_node), .Clr(Clr), .Q(d_flip_flop_1_q[9]));  // open: nQ
  D_flip_flop d_flip_flop_11 (
    .D(_32_bit_input[10]), .CLK(pull_resistor_1_node), .Clr(Clr), .Q(d_flip_flop_1_q[10]));  // open: nQ
  D_flip_flop d_flip_flop_12 (
    .D(_32_bit_input[11]), .CLK(pull_resistor_1_node), .Clr(Clr), .Q(d_flip_flop_1_q[11]));  // open: nQ
  D_flip_flop d_flip_flop_13 (
    .D(_32_bit_input[12]), .CLK(pull_resistor_1_node), .Clr(Clr), .Q(d_flip_flop_1_q[12]));  // open: nQ
  D_flip_flop d_flip_flop_14 (
    .D(_32_bit_input[13]), .CLK(pull_resistor_1_node), .Clr(Clr), .Q(d_flip_flop_1_q[13]));  // open: nQ
  D_flip_flop d_flip_flop_15 (
    .D(_32_bit_input[14]), .CLK(pull_resistor_1_node), .Clr(Clr), .Q(d_flip_flop_1_q[14]));  // open: nQ
  D_flip_flop d_flip_flop_16 (
    .D(_32_bit_input[15]), .CLK(pull_resistor_1_node), .Clr(Clr), .Q(d_flip_flop_1_q[15]));  // open: nQ
  D_flip_flop d_flip_flop_17 (
    .D(_32_bit_input[16]), .CLK(pull_resistor_1_node), .Clr(Clr), .Q(d_flip_flop_1_q[16]));  // open: nQ
  D_flip_flop d_flip_flop_18 (
    .D(_32_bit_input[17]), .CLK(pull_resistor_1_node), .Clr(Clr), .Q(d_flip_flop_1_q[17]));  // open: nQ
  D_flip_flop d_flip_flop_19 (
    .D(_32_bit_input[18]), .CLK(pull_resistor_1_node), .Clr(Clr), .Q(d_flip_flop_1_q[18]));  // open: nQ
  D_flip_flop d_flip_flop_20 (
    .D(_32_bit_input[19]), .CLK(pull_resistor_1_node), .Clr(Clr), .Q(d_flip_flop_1_q[19]));  // open: nQ
  D_flip_flop d_flip_flop_21 (
    .D(_32_bit_input[20]), .CLK(pull_resistor_1_node), .Clr(Clr), .Q(d_flip_flop_1_q[20]));  // open: nQ
  D_flip_flop d_flip_flop_22 (
    .D(_32_bit_input[21]), .CLK(pull_resistor_1_node), .Clr(Clr), .Q(d_flip_flop_1_q[21]));  // open: nQ
  D_flip_flop d_flip_flop_23 (
    .D(_32_bit_input[22]), .CLK(pull_resistor_1_node), .Clr(Clr), .Q(d_flip_flop_1_q[22]));  // open: nQ
  D_flip_flop d_flip_flop_24 (
    .D(_32_bit_input[23]), .CLK(pull_resistor_1_node), .Clr(Clr), .Q(d_flip_flop_1_q[23]));  // open: nQ
  D_flip_flop d_flip_flop_25 (
    .D(_32_bit_input[24]), .CLK(pull_resistor_1_node), .Clr(Clr), .Q(d_flip_flop_1_q[24]));  // open: nQ
  D_flip_flop d_flip_flop_26 (
    .D(_32_bit_input[25]), .CLK(pull_resistor_1_node), .Clr(Clr), .Q(d_flip_flop_1_q[25]));  // open: nQ
  D_flip_flop d_flip_flop_27 (
    .D(_32_bit_input[26]), .CLK(pull_resistor_1_node), .Clr(Clr), .Q(d_flip_flop_1_q[26]));  // open: nQ
  D_flip_flop d_flip_flop_28 (
    .D(_32_bit_input[27]), .CLK(pull_resistor_1_node), .Clr(Clr), .Q(d_flip_flop_1_q[27]));  // open: nQ
  D_flip_flop d_flip_flop_29 (
    .D(_32_bit_input[28]), .CLK(pull_resistor_1_node), .Clr(Clr), .Q(d_flip_flop_1_q[28]));  // open: nQ
  D_flip_flop d_flip_flop_30 (
    .D(_32_bit_input[29]), .CLK(pull_resistor_1_node), .Clr(Clr), .Q(d_flip_flop_1_q[29]));  // open: nQ
  D_flip_flop d_flip_flop_31 (
    .D(_32_bit_input[30]), .CLK(pull_resistor_1_node), .Clr(Clr), .Q(d_flip_flop_1_q[30]));  // open: nQ
  D_flip_flop d_flip_flop_32 (
    .D(_32_bit_input[31]), .CLK(pull_resistor_1_node), .Clr(Clr), .Q(d_flip_flop_1_q[31]));  // open: nQ
  assign _32_bit_output = Ld ? d_flip_flop_1_q : 32'bz;  // Controlled_Buffer controlled_buffer_2
endmodule

module D_flip_flop (
  input  D,
  input  CLK,
  input  Clr,
  output Q,
  output nQ
);

  wire and_1_out, and_2_out, nand_1_out, nand_2_out, not_1_out, not_2_out, not_3_out, not_4_out, not_5_out;

  not not_1 (not_1_out, CLK);
  not not_2 (not_2_out, not_1_out);
  not not_3 (not_3_out, D);
  and and_1 (and_1_out, CLK, not_4_out);
  not not_4 (not_4_out, not_2_out);
  nand nand_1 (nand_1_out, D, and_1_out);
  nand nand_2 (nand_2_out, and_1_out, not_3_out);
  and and_2 (and_2_out, nand_2_out, not_5_out);
  not not_5 (not_5_out, Clr);
  nand nand_3 (Q, nand_1_out, nQ);
  nand nand_4 (nQ, Q, and_2_out);
endmodule
