// Logisim project Full Adder.circ as structural Verilog: 2 circuits, main circuit Full Adder
module Full_Adder (
  input  Cin,
  input  A,
  input  B,
  output S,
  output Cout
);

  wire and_1_out, and_2_out, xor_1_out;

  xor xor_1 (xor_1_out, A, B);
  xor xor_2 (S, Cin, xor_1_out);
  and and_1 (and_1_out, Cin, Cin);
  and and_2 (and_2_out, A, B);
  or or_1 (Cout, and_1_out, and_2_out);
endmodule

module Ripple_adder (
  input  Cin,
  input  A0,
  input  B0,
  input  A1,
  input  B1,
  input  A2,
  input  B2,
  input  A3,
  input  B3,
  output S0,
  output S1,
  output S2,
  output S3,
  output C4
);

  wire full_adder_1_cout, full_adder_2_cout, full_adder_3_cout;

  Full_Adder full_adder_1 (.Cin(Cin), .A(A0), .B(B0), .S(S0), .Cout(full_adder_1_cout));
  Full_Adder full_adder_2 (.Cin(full_adder_1_cout), .A(A1), .B(B1), .S(S1), .Cout(full_adder_2_cout));
  Full_Adder full_adder_3 (.Cin(full_adder_2_cout), .A(A2), .B(B2), .S(S2), .Cout(full_adder_3_cout));
  Full_Adder full_adder_4 (.Cin(full_adder_3_cout), .A(A3), .B(B3), .S(S3), .Cout(C4));

  // Notes on the sheet:
  //   Ripple carry adder
endmodule
