// Logisim project Multiplexer example.circ as structural Verilog: 6 circuits, main circuit Multiplexer example
module Multiplexer_example (
  input  A,
  input  B,
  input  S0,
  input  S1,
  output Out
);

  wire and_1_out_3, not_1_out_2, or_1_out_3, xor_1_out_3;

  AND and_1 (.in_1(A), .in_2(B), .out_3(and_1_out_3));
  OR or_1 (.in_1(A), .in_2(B), .out_3(or_1_out_3));
  NOT not_1 (.in_1(A), .out_2(not_1_out_2));
  XOR xor_1 (.in_1(A), .in_2(B), .out_3(xor_1_out_3));
  Mux mux_1 (.X0(and_1_out_3), .X1(or_1_out_3), .X2(not_1_out_2), .X3(xor_1_out_3), .S0(S0), .S1(S1), .Out(Out));

  // Notes on the sheet:
  //   AND
  //   OR
  //   NOT
  //   XOR
  //   Multiplexer
  //   S1
  //   S2
  //   0
  //   0
  //   1
  //   0
  //   1
  //   0
  //   1
  //   1
  //   Out
  //   AND
  //   OR
  //   NOT
  //   XOR
endmodule

module Mux (
  input  X0,
  input  X1,
  input  X2,
  input  X3,
  input  S0,
  input  S1,
  output Out
);

  wire and_1_out, and_2_out, and_3_out, and_4_out, not_1_out, not_2_out;

  not not_1 (not_1_out, S0);
  not not_2 (not_2_out, S1);
  and and_1 (and_1_out, X0, not_1_out, not_2_out);
  and and_2 (and_2_out, X1, not_1_out, S1);
  and and_3 (and_3_out, X2, S0, not_2_out);
  and and_4 (and_4_out, X3, S0, S1);
  or or_1 (Out, and_1_out, and_2_out, and_3_out, and_4_out);
endmodule

module XOR (
  input  in_1,
  input  in_2,
  output out_3
);

  wire and_1_out, and_2_out, not_1_out, not_2_out;

  not not_1 (not_1_out, in_2);
  not not_2 (not_2_out, in_1);
  and and_1 (and_1_out, in_1, not_1_out);
  and and_2 (and_2_out, not_2_out, in_2);
  or or_1 (out_3, and_1_out, and_2_out);
endmodule

module AND (
  input  in_1,
  input  in_2,
  output out_3
);

  and and_1 (out_3, in_1, in_2);
endmodule

module OR (
  input  in_1,
  input  in_2,
  output out_3
);

  or or_1 (out_3, in_1, in_2);
endmodule

module NOT (
  input  in_1,
  output out_2
);

  not not_1 (out_2, in_1);
endmodule
