// Logisim project Ripple carry Adder.circ as structural Verilog: 4 circuits, main circuit Full Adder
module Ripple_adder_and_CLA (
  input  Cin,
  input  Cin_2,
  input  A0,
  input  B0,
  input  A0_2,
  input  B0_2,
  input  A1,
  input  A1_2,
  input  B1,
  input  B1_2,
  input  A2,
  input  A2_2,
  input  B2,
  input  B2_2,
  input  A3,
  input  A3_2,
  input  B3,
  input  B3_2,
  output S0,
  output S1,
  output S2,
  output S0_2,
  output S1_2,
  output S2_2,
  output S3,
  output S3_2,
  output C4,
  output C4_2
);

  wire full_adder_1_cout, full_adder_2_1_g, full_adder_2_1_p, full_adder_2_2_g, full_adder_2_2_p,
       full_adder_2_3_g, full_adder_2_3_p, full_adder_2_4_g, full_adder_2_4_p, full_adder_2_cout,
       full_adder_3_cout, n4_bit_carry_look_ahead_1_c1, n4_bit_carry_look_ahead_1_c2,
       n4_bit_carry_look_ahead_1_c3;

  Full_Adder full_adder_1 (.Cin(Cin), .A(A0), .B(B0), .S(S0), .Cout(full_adder_1_cout));
  Full_Adder full_adder_2 (.Cin(full_adder_1_cout), .A(A1), .B(B1), .S(S1), .Cout(full_adder_2_cout));
  Full_Adder full_adder_3 (.Cin(full_adder_2_cout), .A(A2), .B(B2), .S(S2), .Cout(full_adder_3_cout));
  Full_Adder full_adder_4 (.Cin(full_adder_3_cout), .A(A3_2), .B(B3_2), .S(S3), .Cout(C4_2));
  Full_adder_2 full_adder_2_1 (.Cin(Cin_2), .A(A0_2), .B(B0_2), .S(S0_2), .G(full_adder_2_1_g), .P(full_adder_2_1_p));
  Full_adder_2 full_adder_2_2 (
    .Cin(n4_bit_carry_look_ahead_1_c1), .A(A1_2), .B(B1_2), .S(S1_2), .G(full_adder_2_2_g),
    .P(full_adder_2_2_p));
  Full_adder_2 full_adder_2_3 (
    .Cin(n4_bit_carry_look_ahead_1_c2), .A(A2_2), .B(B2_2), .S(S2_2), .G(full_adder_2_3_g),
    .P(full_adder_2_3_p));
  Full_adder_2 full_adder_2_4 (
    .Cin(n4_bit_carry_look_ahead_1_c3), .A(A3), .B(B3), .S(S3_2), .G(full_adder_2_4_g), .P(full_adder_2_4_p));
  _4_bit_Carry_look_ahead u_4_bit_carry_look_ahead_1 (
    .Cin(Cin_2), .G0(full_adder_2_1_g), .P0(full_adder_2_1_p), .G1(full_adder_2_2_g), .P1(full_adder_2_2_p),
    .G2(full_adder_2_3_g), .P2(full_adder_2_3_p), .G3(full_adder_2_4_g), .P3(full_adder_2_4_p),
    .C1(n4_bit_carry_look_ahead_1_c1), .C2(n4_bit_carry_look_ahead_1_c2), .C3(n4_bit_carry_look_ahead_1_c3),
    .C4(C4));

  // Notes on the sheet:
  //   Ripple carry adder
  //   Carry lookahead adder
endmodule

module Full_Adder (
  input  Cin,
  input  A,
  input  B,
  output S,
  output Cout
);

  wire and_1_out, and_2_out, xor_1_out;

  xor xor_1 (xor_1_out, A, B);
  xor xor_2 (S, Cin, xor_1_out);
  and and_1 (and_1_out, Cin, xor_1_out);
  and and_2 (and_2_out, A, B);
  or or_1 (Cout, and_1_out, and_2_out);
endmodule

module Full_adder_2 (
  input  Cin,
  input  A,
  input  B,
  output S,
  output G,
  output P
);

  wire xor_1_out;

  xor xor_1 (xor_1_out, A, B);
  xor xor_2 (S, Cin, xor_1_out);
  and and_1 (P, Cin, xor_1_out);
  and and_2 (G, A, B);
endmodule

module _4_bit_Carry_look_ahead (
  input  Cin,
  input  G0,
  input  P0,
  input  G1,
  input  P1,
  input  G2,
  input  P2,
  input  G3,
  input  P3,
  output C1,
  output C2,
  output C3,
  output C4
);

  wire and_1_out, and_2_out, and_3_out, and_4_out;

  and and_1 (and_1_out, P3, C3);
  or or_1 (C4, G3, and_1_out);
  and and_2 (and_2_out, P1, C1);
  or or_2 (C2, G1, and_2_out);
  and and_3 (and_3_out, P2, C2);
  or or_3 (C3, G2, and_3_out);
  and and_4 (and_4_out, P0, Cin);
  or or_4 (C1, G0, and_4_out);
endmodule
