// Logisim project SR flip flop and D flip flop.circ as structural Verilog: 3 circuits, main circuit SR flip flop and D flip flop
module SR_flip_flop_and_D_flip_flop (
  input  S,
  input  D,
  input  R,
  output Q,
  output Q_2,
  output nQ,
  output nQ_2
);

  wire CLK_2_out, CLK_out;

  Clock CLK (.out(CLK_out));
  SR_flip_flop sr_flip_flop_1 (.S(S), .CLK(CLK_out), .R(R), .Q(Q), .nQ(nQ));
  Clock CLK_2 (.out(CLK_2_out));
  D_flip_flop d_flip_flop_1 (.D(D), .CLK(CLK_2_out), .Q(Q_2), .nQ(nQ_2));

  // Notes on the sheet:
  //   SR flip flop
  //   D flip flop
endmodule

module SR_flip_flop (
  input  S,
  input  CLK,
  input  R,
  output Q,
  output nQ
);

  wire nand_1_out, nand_2_out;

  nand nand_1 (nand_1_out, S, CLK);
  nand nand_2 (nand_2_out, CLK, R);
  nand nand_3 (Q, nand_1_out, nQ);
  nand nand_4 (nQ, Q, nand_2_out);
endmodule

module D_flip_flop (
  input  D,
  input  CLK,
  output Q,
  output nQ
);

  wire nand_1_out, nand_2_out, not_1_out;

  not not_1 (not_1_out, D);
  nand nand_1 (nand_1_out, D, CLK);
  nand nand_2 (nand_2_out, CLK, not_1_out);
  nand nand_3 (Q, nand_1_out, nQ);
  nand nand_4 (nQ, Q, nand_2_out);
endmodule
