// Logisim project DMem.circ as structural Verilog: 1 circuit, main circuit main
module main (
  input  [7:0] ADD,
  input  [31:0] DATA_IN,
  input  STR,
  input  CLK,
  input  LD,
  input  CLR,
  output [31:0] OUTPUT
);

  RAM #(.dataWidth(32), .bus("separate")) ram_1 (
    .addr(ADD), .din(DATA_IN), .data(OUTPUT), .str(STR), .sel(1'b1), .clk(CLK), .ld(LD), .clr(CLR));
endmodule
