// Logisim project Decoder1.circ as structural Verilog: 1 circuit, main circuit main
module main (
  input  [31:0] _32_bit_inst,
  output [31:0] inst_1_32,
  output [4:0] inst_33_37
);

  wire not_1_out, not_2_out, not_3_out, not_4_out, not_5_out, not_6_out, not_7_out, not_8_out, not_9_out;

  not not_1 (not_1_out, _32_bit_inst[14]);
  not not_2 (not_2_out, _32_bit_inst[30]);
  not not_3 (not_3_out, _32_bit_inst[13]);
  not not_4 (not_4_out, _32_bit_inst[12]);
  not not_5 (not_5_out, _32_bit_inst[5]);
  not not_6 (not_6_out, _32_bit_inst[6]);
  not not_7 (not_7_out, _32_bit_inst[3]);
  not not_8 (not_8_out, _32_bit_inst[4]);
  not not_9 (not_9_out, _32_bit_inst[2]);
  and BEQ (inst_1_32[26], _32_bit_inst[0], _32_bit_inst[1], not_9_out, not_7_out, not_8_out, _32_bit_inst[5], _32_bit_inst[6], not_4_out, not_3_out, not_1_out);
  and BNE (inst_1_32[27], _32_bit_inst[0], _32_bit_inst[1], not_9_out, not_7_out, not_8_out, _32_bit_inst[5], _32_bit_inst[6], _32_bit_inst[12], not_3_out, not_1_out);
  and BLT (inst_1_32[28], _32_bit_inst[0], _32_bit_inst[1], not_9_out, not_7_out, not_8_out, _32_bit_inst[5], _32_bit_inst[6], not_4_out, not_3_out, _32_bit_inst[14]);
  and BGE (inst_1_32[29], _32_bit_inst[0], _32_bit_inst[1], not_9_out, not_7_out, not_8_out, _32_bit_inst[5], _32_bit_inst[6], _32_bit_inst[12], not_3_out, _32_bit_inst[14]);
  and BLTU (inst_1_32[30], _32_bit_inst[0], _32_bit_inst[1], not_9_out, not_7_out, not_8_out, _32_bit_inst[5], _32_bit_inst[6], not_4_out, _32_bit_inst[13], _32_bit_inst[14]);
  and BGEU (inst_1_32[31], _32_bit_inst[0], _32_bit_inst[1], not_9_out, not_7_out, not_8_out, _32_bit_inst[5], _32_bit_inst[6], _32_bit_inst[12], _32_bit_inst[13], _32_bit_inst[14]);
  and ADDI (inst_1_32[10], _32_bit_inst[0], _32_bit_inst[1], not_9_out, not_7_out, _32_bit_inst[4], not_5_out, not_6_out, not_4_out, not_3_out, not_1_out);
  and ADD (inst_1_32[0], _32_bit_inst[0], _32_bit_inst[1], not_9_out, not_7_out, _32_bit_inst[4], _32_bit_inst[5], not_6_out, not_3_out, not_1_out);
  and LUI (inst_1_32[23], _32_bit_inst[0], _32_bit_inst[1], _32_bit_inst[2], not_7_out, _32_bit_inst[4], not_8_out, not_5_out);
  and AUIPC (inst_1_32[24], _32_bit_inst[0], _32_bit_inst[1], _32_bit_inst[2], not_7_out, _32_bit_inst[4], not_5_out, not_6_out);
  and JAL (inst_1_32[25], _32_bit_inst[0], _32_bit_inst[1], _32_bit_inst[2], _32_bit_inst[3], not_8_out, _32_bit_inst[5], _32_bit_inst[6]);
  and JALR (inst_1_32[11], _32_bit_inst[0], _32_bit_inst[1], _32_bit_inst[2], not_7_out, not_8_out, _32_bit_inst[5], _32_bit_inst[6], not_4_out, not_3_out, not_1_out);
  and SB (inst_1_32[20], _32_bit_inst[0], _32_bit_inst[1], not_9_out, not_7_out, not_8_out, _32_bit_inst[5], not_6_out, not_4_out, not_3_out, not_1_out);
  and SH (inst_1_32[21], _32_bit_inst[0], _32_bit_inst[1], not_9_out, not_7_out, not_8_out, _32_bit_inst[5], not_6_out, _32_bit_inst[12], not_3_out, not_1_out);
  and SW (inst_1_32[22], _32_bit_inst[0], _32_bit_inst[1], not_9_out, not_7_out, not_8_out, _32_bit_inst[5], not_6_out, not_4_out, _32_bit_inst[13], not_1_out);
  and SLTI (inst_1_32[12], _32_bit_inst[0], _32_bit_inst[1], not_9_out, not_7_out, _32_bit_inst[4], not_5_out, not_6_out, not_4_out, _32_bit_inst[13], not_1_out);
  and SLTIU (inst_1_32[13], _32_bit_inst[0], _32_bit_inst[1], not_9_out, not_7_out, _32_bit_inst[4], not_5_out, not_6_out, _32_bit_inst[12], _32_bit_inst[13], not_1_out);
  and XORI (inst_1_32[14], _32_bit_inst[0], _32_bit_inst[1], not_9_out, not_7_out, _32_bit_inst[4], not_5_out, not_6_out, not_4_out, not_3_out, _32_bit_inst[14]);
  and ORI (inst_1_32[15], _32_bit_inst[0], _32_bit_inst[1], not_9_out, not_7_out, _32_bit_inst[4], not_5_out, not_6_out, not_4_out, _32_bit_inst[13], _32_bit_inst[14]);
  and ANDI (inst_1_32[16], _32_bit_inst[0], _32_bit_inst[1], not_9_out, not_7_out, _32_bit_inst[4], not_5_out, not_6_out, not_4_out, not_3_out, _32_bit_inst[14]);
  and SLLI (inst_1_32[17], _32_bit_inst[0], _32_bit_inst[1], not_9_out, not_7_out, _32_bit_inst[4], not_5_out, not_6_out, _32_bit_inst[12], not_3_out, not_1_out);
  and SRLI (inst_1_32[18], _32_bit_inst[0], _32_bit_inst[1], not_9_out, not_7_out, _32_bit_inst[4], not_2_out, not_5_out, not_6_out, _32_bit_inst[12], not_3_out, _32_bit_inst[14]);
  and SRAI (inst_1_32[19], _32_bit_inst[30], _32_bit_inst[0], _32_bit_inst[1], not_9_out, not_7_out, _32_bit_inst[4], not_5_out, not_6_out, _32_bit_inst[12], not_3_out, _32_bit_inst[14]);
  and SUB (inst_1_32[1], _32_bit_inst[30], _32_bit_inst[0], _32_bit_inst[1], not_9_out, not_7_out, _32_bit_inst[4], _32_bit_inst[5], not_6_out, not_4_out, not_3_out, not_1_out);
  and SLL (inst_1_32[2], not_2_out, _32_bit_inst[0], _32_bit_inst[1], not_9_out, not_7_out, _32_bit_inst[4], _32_bit_inst[5], not_6_out, _32_bit_inst[12], not_3_out, not_1_out);
  and SLT (inst_1_32[3], not_2_out, _32_bit_inst[0], _32_bit_inst[1], not_9_out, not_7_out, _32_bit_inst[4], _32_bit_inst[5], not_6_out, not_4_out, _32_bit_inst[13], not_1_out);
  and SLTU (inst_1_32[4], not_2_out, _32_bit_inst[0], _32_bit_inst[1], not_9_out, not_7_out, _32_bit_inst[4], _32_bit_inst[5], not_6_out, _32_bit_inst[6], _32_bit_inst[12], _32_bit_inst[13]);
  and XOR (inst_1_32[5], not_2_out, _32_bit_inst[0], _32_bit_inst[1], not_9_out, not_7_out, _32_bit_inst[4], _32_bit_inst[5], not_6_out, _32_bit_inst[12], not_4_out, not_3_out);
  and SRL (inst_1_32[6], not_2_out, _32_bit_inst[0], _32_bit_inst[1], not_9_out, not_7_out, _32_bit_inst[4], _32_bit_inst[5], not_6_out, _32_bit_inst[12], not_4_out, not_3_out);
  and SRA (inst_1_32[7], _32_bit_inst[30], _32_bit_inst[0], _32_bit_inst[1], not_9_out, not_7_out, _32_bit_inst[4], _32_bit_inst[5], not_6_out, _32_bit_inst[12], not_4_out, not_3_out);
  and OR (inst_1_32[8], not_2_out, _32_bit_inst[0], _32_bit_inst[1], not_9_out, not_7_out, _32_bit_inst[4], _32_bit_inst[5], not_6_out, _32_bit_inst[12], not_4_out, _32_bit_inst[14]);
  and AND (inst_1_32[9], not_2_out, _32_bit_inst[0], _32_bit_inst[1], not_9_out, not_7_out, _32_bit_inst[4], _32_bit_inst[5], not_6_out, _32_bit_inst[12], _32_bit_inst[14], not_4_out);
  and LB (inst_33_37[0], not_1_out, not_3_out, not_4_out, not_6_out, not_5_out, not_8_out, not_7_out, not_9_out, _32_bit_inst[1], _32_bit_inst[0]);
  and LH (inst_33_37[1], not_1_out, not_3_out, _32_bit_inst[12], not_6_out, not_5_out, not_8_out, not_7_out, not_9_out, _32_bit_inst[1], _32_bit_inst[0]);
  and LW (inst_33_37[2], not_1_out, not_4_out, not_4_out, not_6_out, not_5_out, not_8_out, not_7_out, not_9_out, _32_bit_inst[1], _32_bit_inst[0]);
  and LBU (inst_33_37[3], _32_bit_inst[14], not_4_out, not_4_out, not_6_out, not_5_out, not_8_out, not_7_out, not_9_out, _32_bit_inst[1], _32_bit_inst[0]);
  and LHU (inst_33_37[4], _32_bit_inst[14], not_3_out, _32_bit_inst[12], not_6_out, not_5_out, not_8_out, not_7_out, not_9_out, _32_bit_inst[1], _32_bit_inst[0]);
  Pull_Resistor pull_resistor_1 (.node(inst_1_32));

  // Other names for the same wires on the sheet: ADD = inst_1_32[0]; SUB = inst_1_32[1]; SLL = inst_1_32[2];
  //   SLT = inst_1_32[3]; SLTU = inst_1_32[4]; XOR = inst_1_32[5]; SRL = inst_1_32[6]; SRA = inst_1_32[7];
  //   OR = inst_1_32[8]; AND = inst_1_32[9]; ADDI = inst_1_32[10]; JALR = inst_1_32[11]; SLTI = inst_1_32[12];
  //   SLTIU = inst_1_32[13]; XORI = inst_1_32[14]; ORI = inst_1_32[15]; ANDI = inst_1_32[16]; SLLI = inst_1_32[17];
  //   SRLI = inst_1_32[18]; SRAI = inst_1_32[19]; SB = inst_1_32[20]; SH = inst_1_32[21]; SW = inst_1_32[22];
  //   LUI = inst_1_32[23]; AUIPC = inst_1_32[24]; JAL = inst_1_32[25]; BEQ = inst_1_32[26]; BNE = inst_1_32[27];
  //   BLT = inst_1_32[28]; BGE = inst_1_32[29]; BLTU = inst_1_32[30]; BGEU = inst_1_32[31]; LB = inst_33_37[0];
  //   LH = inst_33_37[1]; LW = inst_33_37[2]; LBU = inst_33_37[3]; LHU = inst_33_37[4]
endmodule
