// Logisim project Decoder2.circ as structural Verilog: 1 circuit, main circuit main
module main (
  input  [31:0] inst_1_32,
  input  [4:0] inst_33_37,
  input  [31:0] _32_bit_inst,
  output [6:0] opcode,
  output [4:0] RD,
  output [4:0] RS2,
  output [4:0] RS1,
  output [31:0] IMM
);

  wire I_out, or_1_out, or_2_out, or_3_out, or_4_out, or_5_out, R_out, S_out, SB_out, U_out;
  wire [11:0] controlled_buffer_5_out, controlled_buffer_6_out;
  wire [12:0] controlled_buffer_7_out;
  wire [31:0] controlled_buffer_8_out, controlled_buffer_9_out, pull_resistor_4_node, pull_resistor_5_node,
       pull_resistor_6_node;

  or or_1 (or_1_out, inst_33_37[0], inst_33_37[1], inst_33_37[2], inst_33_37[3], inst_33_37[4]);
  or SB (SB_out, inst_1_32[31], inst_1_32[30], inst_1_32[29], inst_1_32[28], inst_1_32[27], inst_1_32[26]);
  or S (S_out, inst_1_32[22], inst_1_32[21], inst_1_32[20]);
  or U (U_out, inst_1_32[24], inst_1_32[23]);
  or I (I_out, or_1_out, inst_1_32[19], inst_1_32[18], inst_1_32[17], inst_1_32[16], inst_1_32[15], inst_1_32[14], inst_1_32[13], inst_1_32[12], inst_1_32[11], inst_1_32[10]);
  or or_2 (or_2_out, SB_out, S_out, I_out, R_out);
  or R (R_out, inst_1_32[9], inst_1_32[8], inst_1_32[7], inst_1_32[6], inst_1_32[5], inst_1_32[4], inst_1_32[3], inst_1_32[2], inst_1_32[1], inst_1_32[0]);
  or or_3 (or_3_out, SB_out, S_out, R_out);
  or or_4 (or_4_out, SB_out, I_out, R_out);
  or or_5 (or_5_out, SB_out, inst_1_32[25], S_out, I_out, R_out, U_out);
  assign opcode = or_5_out ? _32_bit_inst[6:0] : 7'bz;  // Controlled_Buffer controlled_buffer_1
  assign RD = or_4_out ? _32_bit_inst[19:15] : 5'bz;  // Controlled_Buffer controlled_buffer_2
  Pull_Resistor pull_resistor_1 (.node(RD));
  Pull_Resistor pull_resistor_2 (.node(RS2));
  assign RS2 = or_3_out ? _32_bit_inst[24:20] : 5'bz;  // Controlled_Buffer controlled_buffer_3
  Pull_Resistor pull_resistor_3 (.node(RS1));
  assign RS1 = or_2_out ? _32_bit_inst[11:7] : 5'bz;  // Controlled_Buffer controlled_buffer_4
  assign controlled_buffer_5_out = I_out ? _32_bit_inst[31:20] : 12'bz;  // Controlled_Buffer controlled_buffer_5
  assign controlled_buffer_6_out = S_out ? {_32_bit_inst[31:25], _32_bit_inst[11:7]} : 12'bz;  // Controlled_Buffer controlled_buffer_6
  assign controlled_buffer_7_out = SB_out ? {_32_bit_inst[31], _32_bit_inst[7], _32_bit_inst[30:25], _32_bit_inst[11:8], 1'b0} : 13'bz;  // Controlled_Buffer controlled_buffer_7
  assign controlled_buffer_8_out = U_out ? {_32_bit_inst[31:12], {12{1'b0}}} : 32'bz;  // Controlled_Buffer controlled_buffer_8
  assign controlled_buffer_9_out = inst_1_32[25] ? {{12{_32_bit_inst[31]}}, _32_bit_inst[19:12], _32_bit_inst[20], _32_bit_inst[30:21], 1'b0} : 32'bz;  // Controlled_Buffer controlled_buffer_9
  Pull_Resistor pull_resistor_4 (.node(pull_resistor_4_node));
  assign pull_resistor_4_node = {{20{controlled_buffer_5_out[11]}}, controlled_buffer_5_out};  // Bit_Extender bit_extender_1
  Pull_Resistor pull_resistor_5 (.node(pull_resistor_5_node));
  assign pull_resistor_5_node = {{20{controlled_buffer_6_out[11]}}, controlled_buffer_6_out};  // Bit_Extender bit_extender_2
  Pull_Resistor pull_resistor_6 (.node(pull_resistor_6_node));
  assign pull_resistor_6_node = {{19{controlled_buffer_7_out[12]}}, controlled_buffer_7_out};  // Bit_Extender bit_extender_3
  Pull_Resistor pull_resistor_7 (.node(controlled_buffer_8_out));
  Pull_Resistor pull_resistor_8 (.node(controlled_buffer_9_out));
  assign IMM = pull_resistor_4_node | pull_resistor_5_node | pull_resistor_6_node | controlled_buffer_8_out | controlled_buffer_9_out;  // OR_Gate or_6, 32 bits wide

  // Notes on the sheet:
  //   UJ
  //   IMM
  //   IMM
  //   IMM
  //   IMM
  //   IMM
endmodule
