// Logisim project IMem.circ as structural Verilog: 1 circuit, main circuit main
module main (
  input  [7:0] ADD,
  input  SEL,
  input  CLK,
  input  LD,
  input  CLR,
  output [31:0] OUTPUT
);

  RAM #(.dataWidth(32), .bus("separate")) ram_1 (
    .addr(ADD), .data(OUTPUT), .str(1'b0), .sel(SEL), .clk(CLK), .ld(LD), .clr(CLR));  // open: din
endmodule
