// Logisim project OUTPUTDISPLAY.circ as structural Verilog: 3 circuits, main circuit Output display
module Output_display (
  input  [31:0] ALU_out,
  input  Dmem_rd,
  input  [31:0] Dmem_out,
  input  Output_en,
  input  CLK,
  input  RESET,
  output out_7,
  output out_8,
  output out_9,
  output out_10,
  output out_11,
  output out_12,
  output out_13,
  output out_14,
  output out_15,
  output out_16,
  output out_17,
  output out_18,
  output out_19,
  output out_20,
  output out_21,
  output out_22,
  output out_23,
  output out_24,
  output out_25,
  output out_26,
  output out_27,
  output out_28,
  output out_29,
  output out_30,
  output out_31,
  output out_32,
  output out_33,
  output _6,
  output _4,
  output _2,
  output out_37,
  output out_38,
  output out_39,
  output out_40,
  output out_41,
  output out_42,
  output out_43,
  output out_44,
  output out_45,
  output out_46,
  output out_47,
  output out_48,
  output out_49,
  output out_50,
  output out_51,
  output out_52,
  output out_53,
  output out_54,
  output out_55,
  output out_56,
  output out_57,
  output out_58,
  output out_59,
  output out_60,
  output out_61,
  output out_62,
  output out_63,
  output out_64,
  output out_65,
  output out_66,
  output out_67,
  output out_68,
  output out_69,
  output out_70,
  output out_71,
  output out_72,
  output _7,
  output _5,
  output _3,
  output _1
);

  wire dda_1_lsb_2, dda_1_msb_2, dda_1_out_6, dda_1_out_7, dda_2_lsb_2, dda_2_msb_2, dda_2_out_6,
       dda_2_out_7, dda_3_lsb_2, dda_3_msb_2, dda_3_out_6, dda_3_out_7, dda_4_lsb_2, dda_4_msb_2,
       dda_4_out_6, dda_4_out_7, dda_5_lsb_2, dda_5_msb_2, dda_5_out_6, dda_5_out_7, dda_6_lsb_2,
       dda_6_msb_2, dda_6_out_6, dda_6_out_7, dda_7_lsb_2, dda_7_msb_2, dda_7_out_6, dda_7_out_7,
       dda_8_lsb_2, dda_8_msb_2, dda_8_out_6, dda_8_out_7, dda_9_lsb_2, dda_9_msb_2, dda_9_out_6,
       dda_9_out_7, dda_10_lsb_2, dda_10_msb_2, dda_10_out_6, dda_10_out_7, dda_11_lsb_2, dda_11_msb_2,
       dda_11_out_6, dda_11_out_7, dda_12_lsb_2, dda_12_msb_2, dda_12_out_6, dda_12_out_7, dda_13_lsb_2,
       dda_13_msb_2, dda_13_out_6, dda_13_out_7, dda_14_lsb_2, dda_14_msb_2, dda_14_out_6, dda_14_out_7,
       dda_15_lsb_2, dda_15_msb_2, dda_15_out_6, dda_15_out_7, dda_16_lsb_2, dda_16_msb_2, dda_16_out_6,
       dda_16_out_7, dda_17_lsb_2, dda_17_msb_2, dda_17_out_6, dda_17_out_7, dda_18_lsb_2, dda_18_msb_2,
       dda_18_out_6, dda_18_out_7, dda_19_lsb_2, dda_19_msb_2, dda_19_out_6, dda_19_out_7, dda_20_lsb_2,
       dda_20_msb_2, dda_20_out_6, dda_20_out_7, dda_21_lsb_2, dda_21_msb_2, dda_21_out_6, dda_21_out_7,
       dda_22_lsb_2, dda_22_msb_2, dda_22_out_6, dda_22_out_7, dda_23_lsb_2, dda_23_msb_2, dda_23_out_6,
       dda_23_out_7, dda_24_lsb_2, dda_24_msb_2, dda_24_out_6, dda_24_out_7, dda_25_lsb_2, dda_25_msb_2,
       dda_25_out_6, dda_25_out_7, dda_26_lsb_2, dda_26_msb_2, dda_26_out_6, dda_26_out_7, dda_27_lsb_2,
       dda_27_msb_2, dda_27_out_6, dda_27_out_7, dda_28_lsb_2, dda_28_msb_2, dda_28_out_6, dda_28_out_7,
       dda_29_lsb_2, dda_29_msb_2, dda_29_out_6, dda_29_out_7, dda_30_lsb_2, dda_30_msb_2, dda_30_out_6,
       dda_30_out_7, dda_31_lsb_2, dda_31_msb_2, dda_31_out_6, dda_31_out_7, dda_32_lsb_2, dda_32_msb_2,
       dda_32_out_6, dda_32_out_7, dda_33_lsb_2, dda_33_msb_2, dda_33_out_6, dda_33_out_7, dda_34_lsb_2,
       dda_34_msb_2, dda_34_out_6, dda_34_out_7, dda_35_lsb_2, dda_35_msb_2, dda_35_out_6, dda_35_out_7,
       dda_36_lsb_2, dda_36_msb_2, dda_36_out_6, dda_36_out_7, dda_37_lsb_2, dda_37_msb_2, dda_37_out_6,
       dda_37_out_7, dda_38_lsb_2, dda_38_msb_2, dda_38_out_6, dda_38_out_7, dda_39_lsb_2, dda_39_msb_2,
       dda_39_out_6, dda_39_out_7, dda_40_lsb_2, dda_40_msb_2, dda_40_out_6, dda_40_out_7, dda_41_lsb_2,
       dda_41_msb_2, dda_41_out_6, dda_41_out_7, dda_42_lsb_2, dda_42_msb_2, dda_42_out_6, dda_42_out_7,
       dda_43_lsb_2, dda_43_msb_2, dda_43_out_6, dda_43_out_7, dda_44_lsb_2, dda_44_msb_2, dda_44_out_6,
       dda_44_out_7, dda_45_lsb_2, dda_45_msb_2, dda_45_out_6, dda_45_out_7, dda_46_lsb_2, dda_46_msb_2,
       dda_46_out_6, dda_46_out_7, dda_47_lsb_2, dda_47_msb_2, dda_47_out_6, dda_47_out_7, dda_48_lsb_2,
       dda_48_msb_2, dda_48_out_6, dda_48_out_7, dda_49_lsb_2, dda_49_msb_2, dda_49_out_6, dda_49_out_7,
       dda_50_lsb_2, dda_50_msb_2, dda_50_out_6, dda_50_out_7, dda_51_lsb_2, dda_51_msb_2, dda_51_out_6,
       dda_51_out_7, dda_52_lsb_2, dda_52_msb_2, dda_52_out_6, dda_52_out_7, dda_53_lsb_2, dda_53_msb_2,
       dda_53_out_6, dda_53_out_7, dda_54_lsb_2, dda_54_msb_2, dda_54_out_6, dda_54_out_7, dda_55_lsb_2,
       dda_55_msb_2, dda_55_out_6, dda_55_out_7, dda_56_lsb_2, dda_56_msb_2, dda_56_out_6, dda_56_out_7,
       dda_57_lsb_2, dda_57_msb_2, dda_57_out_6, dda_57_out_7, dda_58_lsb_2, dda_58_msb_2, dda_58_out_6,
       dda_58_out_7, dda_59_lsb_2, dda_59_msb_2, dda_59_out_6, dda_59_out_7, dda_60_lsb_2, dda_60_msb_2,
       dda_60_out_6, dda_60_out_7, dda_61_lsb_2, dda_61_msb_2, dda_61_out_6, dda_61_out_7, dda_62_lsb_2,
       dda_62_msb_2, dda_62_out_6, dda_62_out_7, dda_63_lsb_2, dda_63_msb_2, dda_63_out_6, dda_63_out_7,
       dda_64_lsb_2, dda_64_msb_2, dda_64_out_6, dda_64_out_7, dda_65_lsb_2, dda_65_msb_2, dda_65_out_6,
       dda_65_out_7, dda_66_lsb_2, dda_66_msb_2, dda_66_out_6, dda_66_out_7, dda_67_lsb_2, dda_67_msb_2,
       dda_67_out_6, dda_67_out_7, dda_68_lsb_2, dda_68_msb_2, dda_68_out_6, dda_68_out_7, dda_69_lsb_2,
       dda_69_msb_2, dda_69_out_6, dda_69_out_7, dda_70_lsb_2, dda_70_msb_2, dda_70_out_6, dda_70_out_7,
       dda_71_lsb_2, dda_71_msb_2, dda_71_out_6, dda_71_out_7, dda_72_lsb_2, dda_72_msb_2, dda_72_out_6,
       dda_72_out_7, dda_73_lsb_2, dda_73_msb_2, dda_73_out_6, dda_73_out_7, dda_74_lsb_2, dda_74_msb_2,
       dda_74_out_6, dda_74_out_7, dda_75_lsb_2, dda_75_msb_2, dda_75_out_6, dda_75_out_7, dda_76_lsb_2,
       dda_76_msb_2, dda_76_out_6, dda_76_out_7, dda_77_lsb_2, dda_77_msb_2, dda_77_out_6, dda_77_out_7,
       dda_78_lsb_2, dda_78_msb_2, dda_78_out_6, dda_78_out_7, dda_79_lsb_2, dda_79_msb_2, dda_79_out_6,
       dda_79_out_7, dda_80_lsb_2, dda_80_msb_2, dda_80_out_6, dda_80_out_7, dda_81_lsb_2, dda_81_msb_2,
       dda_81_out_6, dda_81_out_7, dda_82_lsb_2, dda_82_msb_2, dda_82_out_6, dda_82_out_7, dda_83_lsb_2,
       dda_83_msb_2, dda_83_out_6, dda_83_out_7, dda_84_lsb_2, dda_84_msb_2, dda_84_out_6, dda_84_out_7,
       dda_85_lsb_2, dda_85_msb_2, dda_85_out_6, dda_85_out_7, dda_86_lsb_2, dda_86_msb_2, dda_86_out_6,
       dda_86_out_7, dda_87_lsb_2, dda_87_msb_2, dda_87_out_6, dda_87_out_7, dda_88_lsb_2, dda_88_msb_2,
       dda_88_out_6, dda_88_out_7, dda_89_lsb_2, dda_89_msb_2, dda_89_out_6, dda_89_out_7, dda_90_lsb_2,
       dda_90_msb_2, dda_90_out_6, dda_90_out_7, dda_91_lsb_2, dda_91_msb_2, dda_91_out_6, dda_91_out_7,
       dda_92_lsb_2, dda_92_msb_2, dda_92_out_6, dda_92_out_7, dda_93_lsb_2, dda_93_msb_2, dda_93_out_6,
       dda_93_out_7, dda_94_lsb_2, dda_94_msb_2, dda_94_out_6, dda_94_out_7, dda_95_lsb_2, dda_95_msb_2,
       dda_95_out_6, dda_95_out_7, dda_96_lsb_2, dda_96_msb_2, dda_96_out_6, dda_96_out_7, dda_97_lsb_2,
       dda_97_msb_2, dda_97_out_6, dda_97_out_7, dda_98_lsb_2, dda_98_msb_2, dda_98_out_6, dda_98_out_7,
       dda_99_lsb_2, dda_99_msb_2, dda_99_out_6, dda_99_out_7, dda_100_lsb_2, dda_100_msb_2, dda_100_out_6,
       dda_100_out_7, dda_101_lsb_2, dda_101_msb_2, dda_101_out_6, dda_101_out_7, dda_102_lsb_2,
       dda_102_msb_2, dda_102_out_6, dda_102_out_7, dda_103_lsb_2, dda_103_msb_2, dda_103_out_6,
       dda_103_out_7, dda_104_lsb_2, dda_104_msb_2, dda_104_out_6, dda_104_out_7, dda_105_lsb_2,
       dda_105_msb_2, dda_105_out_6, dda_105_out_7, dda_106_lsb_2, dda_106_msb_2, dda_106_out_6,
       dda_106_out_7, dda_107_lsb_2, dda_107_msb_2, dda_107_out_6, dda_107_out_7, dda_108_lsb_2,
       dda_108_msb_2, dda_108_out_6, dda_108_out_7, dda_109_lsb_2, dda_109_msb_2, dda_109_out_6,
       dda_109_out_7, dda_110_lsb_2, dda_110_msb_2, dda_110_out_6, dda_110_out_7, dda_111_lsb_2,
       dda_111_msb_2, dda_111_out_6, dda_111_out_7, dda_112_lsb_2, dda_112_msb_2, dda_112_out_6,
       dda_112_out_7, dda_113_lsb_2, dda_113_msb_2, dda_113_out_6, dda_113_out_7, dda_114_lsb_2,
       dda_114_msb_2, dda_114_out_6, dda_114_out_7, dda_115_lsb_2, dda_115_msb_2, dda_115_out_6,
       dda_115_out_7, dda_116_lsb_2, dda_116_msb_2, dda_116_out_6, dda_116_out_7, dda_117_lsb_2,
       dda_117_msb_2, dda_117_out_6, dda_117_out_7, dda_118_lsb_2, dda_118_msb_2, dda_118_out_6,
       dda_118_out_7, dda_119_lsb_2, dda_119_msb_2, dda_119_out_6, dda_119_out_7, dda_120_lsb_2,
       dda_120_msb_2, dda_120_out_6, dda_120_out_7, dda_121_lsb_2, dda_121_msb_2, dda_121_out_6,
       dda_121_out_7, dda_122_lsb_2, dda_122_msb_2, dda_122_out_6, dda_122_out_7, dda_123_lsb_2,
       dda_123_msb_2, dda_123_out_6, dda_123_out_7, dda_124_lsb_2, dda_124_msb_2, dda_124_out_6,
       dda_124_out_7, dda_125_lsb_2, dda_125_msb_2, dda_125_out_6, dda_125_out_7, dda_126_lsb_2,
       dda_126_msb_2, dda_126_out_6, dda_126_out_7, dda_127_lsb_2, dda_127_msb_2, dda_127_out_6,
       dda_127_out_7, dda_128_lsb_2, dda_128_msb_2, dda_128_out_6, dda_128_out_7, dda_129_lsb_2,
       dda_129_msb_2, dda_129_out_6, dda_129_out_7, dda_130_lsb_2, dda_130_msb_2, dda_130_out_6,
       dda_130_out_7, dda_131_lsb_2, dda_131_msb_2, dda_131_out_6, dda_131_out_7, dda_132_lsb_2,
       dda_132_msb_2, dda_132_out_6, dda_132_out_7, dda_133_lsb_2, dda_133_msb_2, dda_133_out_6,
       dda_133_out_7, dda_134_lsb_2, dda_134_msb_2, dda_134_out_6, dda_134_out_7, dda_135_lsb_2,
       dda_135_msb_2, dda_135_out_6, dda_135_out_7, dda_136_lsb_2, dda_136_msb_2, dda_136_out_6,
       dda_136_out_7, dda_137_lsb_2, dda_137_msb_2, dda_137_out_6, dda_137_out_7, dda_138_lsb_2,
       dda_138_msb_2, dda_138_out_6, dda_138_out_7, dda_139_lsb_2, dda_139_msb_2, dda_139_out_6,
       dda_139_out_7, dda_140_lsb_2, dda_140_msb_2, dda_140_out_6, dda_140_out_7, dda_141_lsb_2,
       dda_141_msb_2, dda_141_out_6, dda_141_out_7, dda_142_lsb_2, dda_142_msb_2, dda_142_out_6,
       dda_142_out_7, dda_143_lsb_2, dda_143_msb_2, dda_143_out_6, dda_143_out_7, dda_144_lsb_2,
       dda_144_msb_2, dda_144_out_6, dda_144_out_7, dda_145_lsb_2, dda_145_msb_2, dda_145_out_6,
       dda_145_out_7, dda_146_lsb_2, dda_146_msb_2, dda_146_out_6, dda_146_out_7, dda_147_lsb_2,
       dda_147_msb_2, dda_147_out_6, dda_147_out_7, dda_148_lsb_2, dda_148_msb_2, dda_148_out_6,
       dda_148_out_7, dda_149_lsb_2, dda_149_msb_2, dda_149_out_6, dda_149_out_7, dda_150_lsb_2,
       dda_150_msb_2, dda_150_out_6, dda_150_out_7, dda_151_lsb_2, dda_151_msb_2, dda_151_out_6,
       dda_151_out_7, dda_152_lsb_2, dda_152_msb_2, dda_152_out_6, dda_152_out_7, dda_153_lsb_2,
       dda_153_out_6, dda_153_out_7, dda_154_lsb_2, dda_154_msb_2, dda_154_out_6, dda_154_out_7,
       dda_155_lsb_2, dda_155_msb_2, dda_155_out_6, dda_155_out_7, dda_156_lsb_2, dda_156_msb_2,
       dda_156_out_6, dda_156_out_7, dda_157_lsb_2, dda_157_msb_2, dda_157_out_6, dda_157_out_7,
       dda_158_lsb_2, dda_158_msb_2, dda_158_out_6, dda_158_out_7, dda_159_lsb_2, dda_159_msb_2,
       dda_159_out_6, dda_159_out_7, dda_160_lsb_2, dda_160_msb_2, dda_160_out_6, dda_160_out_7,
       dda_161_lsb_2, dda_161_msb_2, dda_161_out_6, dda_161_out_7, dda_162_lsb_2, dda_162_msb_2,
       dda_162_out_6, dda_162_out_7, dda_163_lsb_2, dda_163_msb_2, dda_163_out_6, dda_163_out_7,
       dda_164_lsb_2, dda_164_msb_2, dda_164_out_6, dda_164_out_7, dda_165_lsb_2, dda_165_msb_2,
       dda_165_out_6, dda_165_out_7, dda_166_lsb_2, dda_166_msb_2, dda_166_out_6, dda_166_out_7,
       dda_167_lsb_2, dda_167_msb_2, dda_167_out_6, dda_167_out_7, dda_168_lsb_2, dda_168_msb_2,
       dda_168_out_6, dda_168_out_7, dda_169_lsb_2, dda_169_msb_2, dda_169_out_6, dda_169_out_7,
       dda_170_lsb_2, dda_170_out_6, dda_170_out_7, dda_171_lsb_2, dda_171_out_6, dda_171_out_7,
       pull_resistor_1_node;
  wire [3:0] dda_172_msb_2, dda_173_msb_2, dda_174_msb_2, dda_175_msb_2, dda_176_msb_2, dda_177_msb_2,
       dda_178_msb_2, dda_179_msb_2, dda_180_msb_2, register_1_q_2;
  wire [31:0] multiplexer_1_out;
  wire [31:1] register_1_q;

  Multiplexer #(.width(32)) multiplexer_1 (
    .in0(ALU_out), .in1(Dmem_out), .out(multiplexer_1_out), .sel(Dmem_rd), .en(Output_en));
  Register #(.width(32)) register_1 (
    .D(multiplexer_1_out), .Q({register_1_q, register_1_q_2[0]}), .clk(CLK), .clr(RESET));  // open: en
  DDA dda_1 (
    .LSB(pull_resistor_1_node), .in_2(pull_resistor_1_node), .in_3(pull_resistor_1_node),
    .MSB(pull_resistor_1_node), .LSB_2(dda_1_lsb_2), .out_6(dda_1_out_6), .out_7(dda_1_out_7),
    .MSB_2(dda_1_msb_2));
  Pull_Resistor pull_resistor_1 (.node(pull_resistor_1_node));
  DDA dda_2 (
    .LSB(pull_resistor_1_node), .in_2(dda_3_lsb_2), .in_3(dda_3_out_6), .MSB(dda_3_out_7),
    .LSB_2(dda_2_lsb_2), .out_6(dda_2_out_6), .out_7(dda_2_out_7), .MSB_2(dda_2_msb_2));
  DDA dda_3 (
    .LSB(pull_resistor_1_node), .in_2(dda_1_lsb_2), .in_3(dda_1_out_6), .MSB(dda_1_out_7),
    .LSB_2(dda_3_lsb_2), .out_6(dda_3_out_6), .out_7(dda_3_out_7), .MSB_2(dda_3_msb_2));
  DDA dda_4 (
    .LSB(register_1_q[31]), .in_2(dda_5_lsb_2), .in_3(dda_5_out_6), .MSB(dda_5_out_7), .LSB_2(dda_4_lsb_2),
    .out_6(dda_4_out_6), .out_7(dda_4_out_7), .MSB_2(dda_4_msb_2));
  DDA dda_5 (
    .LSB(pull_resistor_1_node), .in_2(dda_6_lsb_2), .in_3(dda_6_out_6), .MSB(dda_6_out_7),
    .LSB_2(dda_5_lsb_2), .out_6(dda_5_out_6), .out_7(dda_5_out_7), .MSB_2(dda_5_msb_2));
  DDA dda_6 (
    .LSB(pull_resistor_1_node), .in_2(dda_2_lsb_2), .in_3(dda_2_out_6), .MSB(dda_2_out_7),
    .LSB_2(dda_6_lsb_2), .out_6(dda_6_out_6), .out_7(dda_6_out_7), .MSB_2(dda_6_msb_2));
  DDA dda_7 (
    .LSB(dda_5_msb_2), .in_2(dda_8_lsb_2), .in_3(dda_8_out_6), .MSB(dda_8_out_7), .LSB_2(dda_7_lsb_2),
    .out_6(dda_7_out_6), .out_7(dda_7_out_7), .MSB_2(dda_7_msb_2));
  DDA dda_8 (
    .LSB(dda_6_msb_2), .in_2(dda_2_msb_2), .in_3(dda_3_msb_2), .MSB(dda_1_msb_2), .LSB_2(dda_8_lsb_2),
    .out_6(dda_8_out_6), .out_7(dda_8_out_7), .MSB_2(dda_8_msb_2));
  DDA dda_9 (
    .LSB(register_1_q[28]), .in_2(dda_10_lsb_2), .in_3(dda_10_out_6), .MSB(dda_10_out_7),
    .LSB_2(dda_9_lsb_2), .out_6(dda_9_out_6), .out_7(dda_9_out_7), .MSB_2(dda_9_msb_2));
  DDA dda_10 (
    .LSB(register_1_q[29]), .in_2(dda_11_lsb_2), .in_3(dda_11_out_6), .MSB(dda_11_out_7),
    .LSB_2(dda_10_lsb_2), .out_6(dda_10_out_6), .out_7(dda_10_out_7), .MSB_2(dda_10_msb_2));
  DDA dda_11 (
    .LSB(register_1_q[30]), .in_2(dda_4_lsb_2), .in_3(dda_4_out_6), .MSB(dda_4_out_7), .LSB_2(dda_11_lsb_2),
    .out_6(dda_11_out_6), .out_7(dda_11_out_7), .MSB_2(dda_11_msb_2));
  DDA dda_12 (
    .LSB(dda_10_msb_2), .in_2(dda_13_lsb_2), .in_3(dda_13_out_6), .MSB(dda_13_out_7), .LSB_2(dda_12_lsb_2),
    .out_6(dda_12_out_6), .out_7(dda_12_out_7), .MSB_2(dda_12_msb_2));
  DDA dda_13 (
    .LSB(dda_11_msb_2), .in_2(dda_14_lsb_2), .in_3(dda_14_out_6), .MSB(dda_14_out_7), .LSB_2(dda_13_lsb_2),
    .out_6(dda_13_out_6), .out_7(dda_13_out_7), .MSB_2(dda_13_msb_2));
  DDA dda_14 (
    .LSB(dda_4_msb_2), .in_2(dda_7_lsb_2), .in_3(dda_7_out_6), .MSB(dda_7_out_7), .LSB_2(dda_14_lsb_2),
    .out_6(dda_14_out_6), .out_7(dda_14_out_7), .MSB_2(dda_14_msb_2));
  DDA dda_15 (
    .LSB(dda_13_msb_2), .in_2(dda_14_msb_2), .in_3(dda_7_msb_2), .MSB(dda_8_msb_2), .LSB_2(dda_15_lsb_2),
    .out_6(dda_15_out_6), .out_7(dda_15_out_7), .MSB_2(dda_15_msb_2));
  DDA dda_16 (
    .LSB(register_1_q[26]), .in_2(dda_17_lsb_2), .in_3(dda_17_out_6), .MSB(dda_17_out_7),
    .LSB_2(dda_16_lsb_2), .out_6(dda_16_out_6), .out_7(dda_16_out_7), .MSB_2(dda_16_msb_2));
  DDA dda_17 (
    .LSB(register_1_q[27]), .in_2(dda_9_lsb_2), .in_3(dda_9_out_6), .MSB(dda_9_out_7), .LSB_2(dda_17_lsb_2),
    .out_6(dda_17_out_6), .out_7(dda_17_out_7), .MSB_2(dda_17_msb_2));
  DDA dda_18 (
    .LSB(dda_17_msb_2), .in_2(dda_19_lsb_2), .in_3(dda_19_out_6), .MSB(dda_19_out_7), .LSB_2(dda_18_lsb_2),
    .out_6(dda_18_out_6), .out_7(dda_18_out_7), .MSB_2(dda_18_msb_2));
  DDA dda_19 (
    .LSB(dda_9_msb_2), .in_2(dda_12_lsb_2), .in_3(dda_12_out_6), .MSB(dda_12_out_7), .LSB_2(dda_19_lsb_2),
    .out_6(dda_19_out_6), .out_7(dda_19_out_7), .MSB_2(dda_19_msb_2));
  DDA dda_20 (
    .LSB(dda_19_msb_2), .in_2(dda_21_lsb_2), .in_3(dda_21_out_6), .MSB(dda_21_out_7), .LSB_2(dda_20_lsb_2),
    .out_6(dda_20_out_6), .out_7(dda_20_out_7), .MSB_2(dda_20_msb_2));
  DDA dda_21 (
    .LSB(dda_12_msb_2), .in_2(dda_15_lsb_2), .in_3(dda_15_out_6), .MSB(dda_15_out_7), .LSB_2(dda_21_lsb_2),
    .out_6(dda_21_out_6), .out_7(dda_21_out_7), .MSB_2(dda_21_msb_2));
  DDA dda_22 (
    .LSB(register_1_q[23]), .in_2(dda_23_lsb_2), .in_3(dda_23_out_6), .MSB(dda_23_out_7),
    .LSB_2(dda_22_lsb_2), .out_6(dda_22_out_6), .out_7(dda_22_out_7), .MSB_2(dda_22_msb_2));
  DDA dda_23 (
    .LSB(register_1_q[24]), .in_2(dda_24_lsb_2), .in_3(dda_24_out_6), .MSB(dda_24_out_7),
    .LSB_2(dda_23_lsb_2), .out_6(dda_23_out_6), .out_7(dda_23_out_7), .MSB_2(dda_23_msb_2));
  DDA dda_24 (
    .LSB(register_1_q[25]), .in_2(dda_16_lsb_2), .in_3(dda_16_out_6), .MSB(dda_16_out_7),
    .LSB_2(dda_24_lsb_2), .out_6(dda_24_out_6), .out_7(dda_24_out_7), .MSB_2(dda_24_msb_2));
  DDA dda_25 (
    .LSB(dda_23_msb_2), .in_2(dda_26_lsb_2), .in_3(dda_26_out_6), .MSB(dda_26_out_7), .LSB_2(dda_25_lsb_2),
    .out_6(dda_25_out_6), .out_7(dda_25_out_7), .MSB_2(dda_25_msb_2));
  DDA dda_26 (
    .LSB(dda_24_msb_2), .in_2(dda_27_lsb_2), .in_3(dda_27_out_6), .MSB(dda_27_out_7), .LSB_2(dda_26_lsb_2),
    .out_6(dda_26_out_6), .out_7(dda_26_out_7), .MSB_2(dda_26_msb_2));
  DDA dda_27 (
    .LSB(dda_16_msb_2), .in_2(dda_18_lsb_2), .in_3(dda_18_out_6), .MSB(dda_18_out_7), .LSB_2(dda_27_lsb_2),
    .out_6(dda_27_out_6), .out_7(dda_27_out_7), .MSB_2(dda_27_msb_2));
  DDA dda_28 (
    .LSB(dda_26_msb_2), .in_2(dda_29_lsb_2), .in_3(dda_29_out_6), .MSB(dda_29_out_7), .LSB_2(dda_28_lsb_2),
    .out_6(dda_28_out_6), .out_7(dda_28_out_7), .MSB_2(dda_28_msb_2));
  DDA dda_29 (
    .LSB(dda_27_msb_2), .in_2(dda_30_lsb_2), .in_3(dda_30_out_6), .MSB(dda_30_out_7), .LSB_2(dda_29_lsb_2),
    .out_6(dda_29_out_6), .out_7(dda_29_out_7), .MSB_2(dda_29_msb_2));
  DDA dda_30 (
    .LSB(dda_18_msb_2), .in_2(dda_20_lsb_2), .in_3(dda_20_out_6), .MSB(dda_20_out_7), .LSB_2(dda_30_lsb_2),
    .out_6(dda_30_out_6), .out_7(dda_30_out_7), .MSB_2(dda_30_msb_2));
  DDA dda_31 (
    .LSB(dda_29_msb_2), .in_2(dda_32_lsb_2), .in_3(dda_32_out_6), .MSB(dda_32_out_7), .LSB_2(dda_31_lsb_2),
    .out_6(dda_31_out_6), .out_7(dda_31_out_7), .MSB_2(dda_31_msb_2));
  DDA dda_32 (
    .LSB(dda_30_msb_2), .in_2(dda_20_msb_2), .in_3(dda_21_msb_2), .MSB(dda_15_msb_2), .LSB_2(dda_32_lsb_2),
    .out_6(dda_32_out_6), .out_7(dda_32_out_7), .MSB_2(dda_32_msb_2));
  DDA dda_33 (
    .LSB(register_1_q[20]), .in_2(dda_34_lsb_2), .in_3(dda_34_out_6), .MSB(dda_34_out_7),
    .LSB_2(dda_33_lsb_2), .out_6(dda_33_out_6), .out_7(dda_33_out_7), .MSB_2(dda_33_msb_2));
  DDA dda_34 (
    .LSB(register_1_q[21]), .in_2(dda_35_lsb_2), .in_3(dda_35_out_6), .MSB(dda_35_out_7),
    .LSB_2(dda_34_lsb_2), .out_6(dda_34_out_6), .out_7(dda_34_out_7), .MSB_2(dda_34_msb_2));
  DDA dda_35 (
    .LSB(register_1_q[22]), .in_2(dda_22_lsb_2), .in_3(dda_22_out_6), .MSB(dda_22_out_7),
    .LSB_2(dda_35_lsb_2), .out_6(dda_35_out_6), .out_7(dda_35_out_7), .MSB_2(dda_35_msb_2));
  DDA dda_36 (
    .LSB(dda_34_msb_2), .in_2(dda_37_lsb_2), .in_3(dda_37_out_6), .MSB(dda_37_out_7), .LSB_2(dda_36_lsb_2),
    .out_6(dda_36_out_6), .out_7(dda_36_out_7), .MSB_2(dda_36_msb_2));
  DDA dda_37 (
    .LSB(dda_35_msb_2), .in_2(dda_38_lsb_2), .in_3(dda_38_out_6), .MSB(dda_38_out_7), .LSB_2(dda_37_lsb_2),
    .out_6(dda_37_out_6), .out_7(dda_37_out_7), .MSB_2(dda_37_msb_2));
  DDA dda_38 (
    .LSB(dda_22_msb_2), .in_2(dda_25_lsb_2), .in_3(dda_25_out_6), .MSB(dda_25_out_7), .LSB_2(dda_38_lsb_2),
    .out_6(dda_38_out_6), .out_7(dda_38_out_7), .MSB_2(dda_38_msb_2));
  DDA dda_39 (
    .LSB(dda_37_msb_2), .in_2(dda_40_lsb_2), .in_3(dda_40_out_6), .MSB(dda_40_out_7), .LSB_2(dda_39_lsb_2),
    .out_6(dda_39_out_6), .out_7(dda_39_out_7), .MSB_2(dda_39_msb_2));
  DDA dda_40 (
    .LSB(dda_38_msb_2), .in_2(dda_41_lsb_2), .in_3(dda_41_out_6), .MSB(dda_41_out_7), .LSB_2(dda_40_lsb_2),
    .out_6(dda_40_out_6), .out_7(dda_40_out_7), .MSB_2(dda_40_msb_2));
  DDA dda_41 (
    .LSB(dda_25_msb_2), .in_2(dda_28_lsb_2), .in_3(dda_28_out_6), .MSB(dda_28_out_7), .LSB_2(dda_41_lsb_2),
    .out_6(dda_41_out_6), .out_7(dda_41_out_7), .MSB_2(dda_41_msb_2));
  DDA dda_42 (
    .LSB(dda_40_msb_2), .in_2(dda_43_lsb_2), .in_3(dda_43_out_6), .MSB(dda_43_out_7), .LSB_2(dda_42_lsb_2),
    .out_6(dda_42_out_6), .out_7(dda_42_out_7), .MSB_2(dda_42_msb_2));
  DDA dda_43 (
    .LSB(dda_41_msb_2), .in_2(dda_44_lsb_2), .in_3(dda_44_out_6), .MSB(dda_44_out_7), .LSB_2(dda_43_lsb_2),
    .out_6(dda_43_out_6), .out_7(dda_43_out_7), .MSB_2(dda_43_msb_2));
  DDA dda_44 (
    .LSB(dda_28_msb_2), .in_2(dda_31_lsb_2), .in_3(dda_31_out_6), .MSB(dda_31_out_7), .LSB_2(dda_44_lsb_2),
    .out_6(dda_44_out_6), .out_7(dda_44_out_7), .MSB_2(dda_44_msb_2));
  DDA dda_45 (
    .LSB(dda_43_msb_2), .in_2(dda_44_msb_2), .in_3(dda_31_msb_2), .MSB(dda_32_msb_2), .LSB_2(dda_45_lsb_2),
    .out_6(dda_45_out_6), .out_7(dda_45_out_7), .MSB_2(dda_45_msb_2));
  DDA dda_46 (
    .LSB(register_1_q[18]), .in_2(dda_47_lsb_2), .in_3(dda_47_out_6), .MSB(dda_47_out_7),
    .LSB_2(dda_46_lsb_2), .out_6(dda_46_out_6), .out_7(dda_46_out_7), .MSB_2(dda_46_msb_2));
  DDA dda_47 (
    .LSB(register_1_q[19]), .in_2(dda_33_lsb_2), .in_3(dda_33_out_6), .MSB(dda_33_out_7),
    .LSB_2(dda_47_lsb_2), .out_6(dda_47_out_6), .out_7(dda_47_out_7), .MSB_2(dda_47_msb_2));
  DDA dda_48 (
    .LSB(dda_47_msb_2), .in_2(dda_49_lsb_2), .in_3(dda_49_out_6), .MSB(dda_49_out_7), .LSB_2(dda_48_lsb_2),
    .out_6(dda_48_out_6), .out_7(dda_48_out_7), .MSB_2(dda_48_msb_2));
  DDA dda_49 (
    .LSB(dda_33_msb_2), .in_2(dda_36_lsb_2), .in_3(dda_36_out_6), .MSB(dda_36_out_7), .LSB_2(dda_49_lsb_2),
    .out_6(dda_49_out_6), .out_7(dda_49_out_7), .MSB_2(dda_49_msb_2));
  DDA dda_50 (
    .LSB(dda_49_msb_2), .in_2(dda_51_lsb_2), .in_3(dda_51_out_6), .MSB(dda_51_out_7), .LSB_2(dda_50_lsb_2),
    .out_6(dda_50_out_6), .out_7(dda_50_out_7), .MSB_2(dda_50_msb_2));
  DDA dda_51 (
    .LSB(dda_36_msb_2), .in_2(dda_39_lsb_2), .in_3(dda_39_out_6), .MSB(dda_39_out_7), .LSB_2(dda_51_lsb_2),
    .out_6(dda_51_out_6), .out_7(dda_51_out_7), .MSB_2(dda_51_msb_2));
  DDA dda_52 (
    .LSB(dda_51_msb_2), .in_2(dda_53_lsb_2), .in_3(dda_53_out_6), .MSB(dda_53_out_7), .LSB_2(dda_52_lsb_2),
    .out_6(dda_52_out_6), .out_7(dda_52_out_7), .MSB_2(dda_52_msb_2));
  DDA dda_53 (
    .LSB(dda_39_msb_2), .in_2(dda_42_lsb_2), .in_3(dda_42_out_6), .MSB(dda_42_out_7), .LSB_2(dda_53_lsb_2),
    .out_6(dda_53_out_6), .out_7(dda_53_out_7), .MSB_2(dda_53_msb_2));
  DDA dda_54 (
    .LSB(dda_53_msb_2), .in_2(dda_55_lsb_2), .in_3(dda_55_out_6), .MSB(dda_55_out_7), .LSB_2(dda_54_lsb_2),
    .out_6(dda_54_out_6), .out_7(dda_54_out_7), .MSB_2(dda_54_msb_2));
  DDA dda_55 (
    .LSB(dda_42_msb_2), .in_2(dda_45_lsb_2), .in_3(dda_45_out_6), .MSB(dda_45_out_7), .LSB_2(dda_55_lsb_2),
    .out_6(dda_55_out_6), .out_7(dda_55_out_7), .MSB_2(dda_55_msb_2));
  DDA dda_56 (
    .LSB(register_1_q[15]), .in_2(dda_57_lsb_2), .in_3(dda_57_out_6), .MSB(dda_57_out_7),
    .LSB_2(dda_56_lsb_2), .out_6(dda_56_out_6), .out_7(dda_56_out_7), .MSB_2(dda_56_msb_2));
  DDA dda_57 (
    .LSB(register_1_q[16]), .in_2(dda_58_lsb_2), .in_3(dda_58_out_6), .MSB(dda_58_out_7),
    .LSB_2(dda_57_lsb_2), .out_6(dda_57_out_6), .out_7(dda_57_out_7), .MSB_2(dda_57_msb_2));
  DDA dda_58 (
    .LSB(register_1_q[17]), .in_2(dda_46_lsb_2), .in_3(dda_46_out_6), .MSB(dda_46_out_7),
    .LSB_2(dda_58_lsb_2), .out_6(dda_58_out_6), .out_7(dda_58_out_7), .MSB_2(dda_58_msb_2));
  DDA dda_59 (
    .LSB(dda_57_msb_2), .in_2(dda_60_lsb_2), .in_3(dda_60_out_6), .MSB(dda_60_out_7), .LSB_2(dda_59_lsb_2),
    .out_6(dda_59_out_6), .out_7(dda_59_out_7), .MSB_2(dda_59_msb_2));
  DDA dda_60 (
    .LSB(dda_58_msb_2), .in_2(dda_61_lsb_2), .in_3(dda_61_out_6), .MSB(dda_61_out_7), .LSB_2(dda_60_lsb_2),
    .out_6(dda_60_out_6), .out_7(dda_60_out_7), .MSB_2(dda_60_msb_2));
  DDA dda_61 (
    .LSB(dda_46_msb_2), .in_2(dda_48_lsb_2), .in_3(dda_48_out_6), .MSB(dda_48_out_7), .LSB_2(dda_61_lsb_2),
    .out_6(dda_61_out_6), .out_7(dda_61_out_7), .MSB_2(dda_61_msb_2));
  DDA dda_62 (
    .LSB(dda_60_msb_2), .in_2(dda_63_lsb_2), .in_3(dda_63_out_6), .MSB(dda_63_out_7), .LSB_2(dda_62_lsb_2),
    .out_6(dda_62_out_6), .out_7(dda_62_out_7), .MSB_2(dda_62_msb_2));
  DDA dda_63 (
    .LSB(dda_61_msb_2), .in_2(dda_64_lsb_2), .in_3(dda_64_out_6), .MSB(dda_64_out_7), .LSB_2(dda_63_lsb_2),
    .out_6(dda_63_out_6), .out_7(dda_63_out_7), .MSB_2(dda_63_msb_2));
  DDA dda_64 (
    .LSB(dda_48_msb_2), .in_2(dda_50_lsb_2), .in_3(dda_50_out_6), .MSB(dda_50_out_7), .LSB_2(dda_64_lsb_2),
    .out_6(dda_64_out_6), .out_7(dda_64_out_7), .MSB_2(dda_64_msb_2));
  DDA dda_65 (
    .LSB(dda_63_msb_2), .in_2(dda_66_lsb_2), .in_3(dda_66_out_6), .MSB(dda_66_out_7), .LSB_2(dda_65_lsb_2),
    .out_6(dda_65_out_6), .out_7(dda_65_out_7), .MSB_2(dda_65_msb_2));
  DDA dda_66 (
    .LSB(dda_64_msb_2), .in_2(dda_67_lsb_2), .in_3(dda_67_out_6), .MSB(dda_67_out_7), .LSB_2(dda_66_lsb_2),
    .out_6(dda_66_out_6), .out_7(dda_66_out_7), .MSB_2(dda_66_msb_2));
  DDA dda_67 (
    .LSB(dda_50_msb_2), .in_2(dda_52_lsb_2), .in_3(dda_52_out_6), .MSB(dda_52_out_7), .LSB_2(dda_67_lsb_2),
    .out_6(dda_67_out_6), .out_7(dda_67_out_7), .MSB_2(dda_67_msb_2));
  DDA dda_68 (
    .LSB(dda_66_msb_2), .in_2(dda_69_lsb_2), .in_3(dda_69_out_6), .MSB(dda_69_out_7), .LSB_2(dda_68_lsb_2),
    .out_6(dda_68_out_6), .out_7(dda_68_out_7), .MSB_2(dda_68_msb_2));
  DDA dda_69 (
    .LSB(dda_67_msb_2), .in_2(dda_70_lsb_2), .in_3(dda_70_out_6), .MSB(dda_70_out_7), .LSB_2(dda_69_lsb_2),
    .out_6(dda_69_out_6), .out_7(dda_69_out_7), .MSB_2(dda_69_msb_2));
  DDA dda_70 (
    .LSB(dda_52_msb_2), .in_2(dda_54_lsb_2), .in_3(dda_54_out_6), .MSB(dda_54_out_7), .LSB_2(dda_70_lsb_2),
    .out_6(dda_70_out_6), .out_7(dda_70_out_7), .MSB_2(dda_70_msb_2));
  DDA dda_71 (
    .LSB(dda_69_msb_2), .in_2(dda_72_lsb_2), .in_3(dda_72_out_6), .MSB(dda_72_out_7), .LSB_2(dda_71_lsb_2),
    .out_6(dda_71_out_6), .out_7(dda_71_out_7), .MSB_2(dda_71_msb_2));
  DDA dda_72 (
    .LSB(dda_70_msb_2), .in_2(dda_54_msb_2), .in_3(dda_55_msb_2), .MSB(dda_45_msb_2), .LSB_2(dda_72_lsb_2),
    .out_6(dda_72_out_6), .out_7(dda_72_out_7), .MSB_2(dda_72_msb_2));
  DDA dda_73 (
    .LSB(register_1_q[12]), .in_2(dda_74_lsb_2), .in_3(dda_74_out_6), .MSB(dda_74_out_7),
    .LSB_2(dda_73_lsb_2), .out_6(dda_73_out_6), .out_7(dda_73_out_7), .MSB_2(dda_73_msb_2));
  DDA dda_74 (
    .LSB(register_1_q[13]), .in_2(dda_75_lsb_2), .in_3(dda_75_out_6), .MSB(dda_75_out_7),
    .LSB_2(dda_74_lsb_2), .out_6(dda_74_out_6), .out_7(dda_74_out_7), .MSB_2(dda_74_msb_2));
  DDA dda_75 (
    .LSB(register_1_q[14]), .in_2(dda_56_lsb_2), .in_3(dda_56_out_6), .MSB(dda_56_out_7),
    .LSB_2(dda_75_lsb_2), .out_6(dda_75_out_6), .out_7(dda_75_out_7), .MSB_2(dda_75_msb_2));
  DDA dda_76 (
    .LSB(dda_74_msb_2), .in_2(dda_77_lsb_2), .in_3(dda_77_out_6), .MSB(dda_77_out_7), .LSB_2(dda_76_lsb_2),
    .out_6(dda_76_out_6), .out_7(dda_76_out_7), .MSB_2(dda_76_msb_2));
  DDA dda_77 (
    .LSB(dda_75_msb_2), .in_2(dda_78_lsb_2), .in_3(dda_78_out_6), .MSB(dda_78_out_7), .LSB_2(dda_77_lsb_2),
    .out_6(dda_77_out_6), .out_7(dda_77_out_7), .MSB_2(dda_77_msb_2));
  DDA dda_78 (
    .LSB(dda_56_msb_2), .in_2(dda_59_lsb_2), .in_3(dda_59_out_6), .MSB(dda_59_out_7), .LSB_2(dda_78_lsb_2),
    .out_6(dda_78_out_6), .out_7(dda_78_out_7), .MSB_2(dda_78_msb_2));
  DDA dda_79 (
    .LSB(dda_77_msb_2), .in_2(dda_80_lsb_2), .in_3(dda_80_out_6), .MSB(dda_80_out_7), .LSB_2(dda_79_lsb_2),
    .out_6(dda_79_out_6), .out_7(dda_79_out_7), .MSB_2(dda_79_msb_2));
  DDA dda_80 (
    .LSB(dda_78_msb_2), .in_2(dda_81_lsb_2), .in_3(dda_81_out_6), .MSB(dda_81_out_7), .LSB_2(dda_80_lsb_2),
    .out_6(dda_80_out_6), .out_7(dda_80_out_7), .MSB_2(dda_80_msb_2));
  DDA dda_81 (
    .LSB(dda_59_msb_2), .in_2(dda_62_lsb_2), .in_3(dda_62_out_6), .MSB(dda_62_out_7), .LSB_2(dda_81_lsb_2),
    .out_6(dda_81_out_6), .out_7(dda_81_out_7), .MSB_2(dda_81_msb_2));
  DDA dda_82 (
    .LSB(dda_80_msb_2), .in_2(dda_83_lsb_2), .in_3(dda_83_out_6), .MSB(dda_83_out_7), .LSB_2(dda_82_lsb_2),
    .out_6(dda_82_out_6), .out_7(dda_82_out_7), .MSB_2(dda_82_msb_2));
  DDA dda_83 (
    .LSB(dda_81_msb_2), .in_2(dda_84_lsb_2), .in_3(dda_84_out_6), .MSB(dda_84_out_7), .LSB_2(dda_83_lsb_2),
    .out_6(dda_83_out_6), .out_7(dda_83_out_7), .MSB_2(dda_83_msb_2));
  DDA dda_84 (
    .LSB(dda_62_msb_2), .in_2(dda_65_lsb_2), .in_3(dda_65_out_6), .MSB(dda_65_out_7), .LSB_2(dda_84_lsb_2),
    .out_6(dda_84_out_6), .out_7(dda_84_out_7), .MSB_2(dda_84_msb_2));
  DDA dda_85 (
    .LSB(dda_83_msb_2), .in_2(dda_86_lsb_2), .in_3(dda_86_out_6), .MSB(dda_86_out_7), .LSB_2(dda_85_lsb_2),
    .out_6(dda_85_out_6), .out_7(dda_85_out_7), .MSB_2(dda_85_msb_2));
  DDA dda_86 (
    .LSB(dda_84_msb_2), .in_2(dda_87_lsb_2), .in_3(dda_87_out_6), .MSB(dda_87_out_7), .LSB_2(dda_86_lsb_2),
    .out_6(dda_86_out_6), .out_7(dda_86_out_7), .MSB_2(dda_86_msb_2));
  DDA dda_87 (
    .LSB(dda_65_msb_2), .in_2(dda_68_lsb_2), .in_3(dda_68_out_6), .MSB(dda_68_out_7), .LSB_2(dda_87_lsb_2),
    .out_6(dda_87_out_6), .out_7(dda_87_out_7), .MSB_2(dda_87_msb_2));
  DDA dda_88 (
    .LSB(dda_86_msb_2), .in_2(dda_89_lsb_2), .in_3(dda_89_out_6), .MSB(dda_89_out_7), .LSB_2(dda_88_lsb_2),
    .out_6(dda_88_out_6), .out_7(dda_88_out_7), .MSB_2(dda_88_msb_2));
  DDA dda_89 (
    .LSB(dda_87_msb_2), .in_2(dda_90_lsb_2), .in_3(dda_90_out_6), .MSB(dda_90_out_7), .LSB_2(dda_89_lsb_2),
    .out_6(dda_89_out_6), .out_7(dda_89_out_7), .MSB_2(dda_89_msb_2));
  DDA dda_90 (
    .LSB(dda_68_msb_2), .in_2(dda_71_lsb_2), .in_3(dda_71_out_6), .MSB(dda_71_out_7), .LSB_2(dda_90_lsb_2),
    .out_6(dda_90_out_6), .out_7(dda_90_out_7), .MSB_2(dda_90_msb_2));
  DDA dda_91 (
    .LSB(dda_89_msb_2), .in_2(dda_90_msb_2), .in_3(dda_71_msb_2), .MSB(dda_72_msb_2), .LSB_2(dda_91_lsb_2),
    .out_6(dda_91_out_6), .out_7(dda_91_out_7), .MSB_2(dda_91_msb_2));
  DDA dda_92 (
    .LSB(register_1_q[10]), .in_2(dda_93_lsb_2), .in_3(dda_93_out_6), .MSB(dda_93_out_7),
    .LSB_2(dda_92_lsb_2), .out_6(dda_92_out_6), .out_7(dda_92_out_7), .MSB_2(dda_92_msb_2));
  DDA dda_93 (
    .LSB(register_1_q[11]), .in_2(dda_73_lsb_2), .in_3(dda_73_out_6), .MSB(dda_73_out_7),
    .LSB_2(dda_93_lsb_2), .out_6(dda_93_out_6), .out_7(dda_93_out_7), .MSB_2(dda_93_msb_2));
  DDA dda_94 (
    .LSB(dda_93_msb_2), .in_2(dda_95_lsb_2), .in_3(dda_95_out_6), .MSB(dda_95_out_7), .LSB_2(dda_94_lsb_2),
    .out_6(dda_94_out_6), .out_7(dda_94_out_7), .MSB_2(dda_94_msb_2));
  DDA dda_95 (
    .LSB(dda_73_msb_2), .in_2(dda_76_lsb_2), .in_3(dda_76_out_6), .MSB(dda_76_out_7), .LSB_2(dda_95_lsb_2),
    .out_6(dda_95_out_6), .out_7(dda_95_out_7), .MSB_2(dda_95_msb_2));
  DDA dda_96 (
    .LSB(dda_95_msb_2), .in_2(dda_97_lsb_2), .in_3(dda_97_out_6), .MSB(dda_97_out_7), .LSB_2(dda_96_lsb_2),
    .out_6(dda_96_out_6), .out_7(dda_96_out_7), .MSB_2(dda_96_msb_2));
  DDA dda_97 (
    .LSB(dda_76_msb_2), .in_2(dda_79_lsb_2), .in_3(dda_79_out_6), .MSB(dda_79_out_7), .LSB_2(dda_97_lsb_2),
    .out_6(dda_97_out_6), .out_7(dda_97_out_7), .MSB_2(dda_97_msb_2));
  DDA dda_98 (
    .LSB(dda_97_msb_2), .in_2(dda_99_lsb_2), .in_3(dda_99_out_6), .MSB(dda_99_out_7), .LSB_2(dda_98_lsb_2),
    .out_6(dda_98_out_6), .out_7(dda_98_out_7), .MSB_2(dda_98_msb_2));
  DDA dda_99 (
    .LSB(dda_79_msb_2), .in_2(dda_82_lsb_2), .in_3(dda_82_out_6), .MSB(dda_82_out_7), .LSB_2(dda_99_lsb_2),
    .out_6(dda_99_out_6), .out_7(dda_99_out_7), .MSB_2(dda_99_msb_2));
  DDA dda_100 (
    .LSB(dda_99_msb_2), .in_2(dda_101_lsb_2), .in_3(dda_101_out_6), .MSB(dda_101_out_7),
    .LSB_2(dda_100_lsb_2), .out_6(dda_100_out_6), .out_7(dda_100_out_7), .MSB_2(dda_100_msb_2));
  DDA dda_101 (
    .LSB(dda_82_msb_2), .in_2(dda_85_lsb_2), .in_3(dda_85_out_6), .MSB(dda_85_out_7), .LSB_2(dda_101_lsb_2),
    .out_6(dda_101_out_6), .out_7(dda_101_out_7), .MSB_2(dda_101_msb_2));
  DDA dda_102 (
    .LSB(dda_101_msb_2), .in_2(dda_103_lsb_2), .in_3(dda_103_out_6), .MSB(dda_103_out_7),
    .LSB_2(dda_102_lsb_2), .out_6(dda_102_out_6), .out_7(dda_102_out_7), .MSB_2(dda_102_msb_2));
  DDA dda_103 (
    .LSB(dda_85_msb_2), .in_2(dda_88_lsb_2), .in_3(dda_88_out_6), .MSB(dda_88_out_7), .LSB_2(dda_103_lsb_2),
    .out_6(dda_103_out_6), .out_7(dda_103_out_7), .MSB_2(dda_103_msb_2));
  DDA dda_104 (
    .LSB(dda_103_msb_2), .in_2(dda_105_lsb_2), .in_3(dda_105_out_6), .MSB(dda_105_out_7),
    .LSB_2(dda_104_lsb_2), .out_6(dda_104_out_6), .out_7(dda_104_out_7), .MSB_2(dda_104_msb_2));
  DDA dda_105 (
    .LSB(dda_88_msb_2), .in_2(dda_91_lsb_2), .in_3(dda_91_out_6), .MSB(dda_91_out_7), .LSB_2(dda_105_lsb_2),
    .out_6(dda_105_out_6), .out_7(dda_105_out_7), .MSB_2(dda_105_msb_2));
  DDA dda_106 (
    .LSB(register_1_q[7]), .in_2(dda_107_lsb_2), .in_3(dda_107_out_6), .MSB(dda_107_out_7),
    .LSB_2(dda_106_lsb_2), .out_6(dda_106_out_6), .out_7(dda_106_out_7), .MSB_2(dda_106_msb_2));
  DDA dda_107 (
    .LSB(register_1_q[8]), .in_2(dda_108_lsb_2), .in_3(dda_108_out_6), .MSB(dda_108_out_7),
    .LSB_2(dda_107_lsb_2), .out_6(dda_107_out_6), .out_7(dda_107_out_7), .MSB_2(dda_107_msb_2));
  DDA dda_108 (
    .LSB(register_1_q[9]), .in_2(dda_92_lsb_2), .in_3(dda_92_out_6), .MSB(dda_92_out_7),
    .LSB_2(dda_108_lsb_2), .out_6(dda_108_out_6), .out_7(dda_108_out_7), .MSB_2(dda_108_msb_2));
  DDA dda_109 (
    .LSB(dda_107_msb_2), .in_2(dda_110_lsb_2), .in_3(dda_110_out_6), .MSB(dda_110_out_7),
    .LSB_2(dda_109_lsb_2), .out_6(dda_109_out_6), .out_7(dda_109_out_7), .MSB_2(dda_109_msb_2));
  DDA dda_110 (
    .LSB(dda_108_msb_2), .in_2(dda_111_lsb_2), .in_3(dda_111_out_6), .MSB(dda_111_out_7),
    .LSB_2(dda_110_lsb_2), .out_6(dda_110_out_6), .out_7(dda_110_out_7), .MSB_2(dda_110_msb_2));
  DDA dda_111 (
    .LSB(dda_92_msb_2), .in_2(dda_94_lsb_2), .in_3(dda_94_out_6), .MSB(dda_94_out_7), .LSB_2(dda_111_lsb_2),
    .out_6(dda_111_out_6), .out_7(dda_111_out_7), .MSB_2(dda_111_msb_2));
  DDA dda_112 (
    .LSB(dda_110_msb_2), .in_2(dda_113_lsb_2), .in_3(dda_113_out_6), .MSB(dda_113_out_7),
    .LSB_2(dda_112_lsb_2), .out_6(dda_112_out_6), .out_7(dda_112_out_7), .MSB_2(dda_112_msb_2));
  DDA dda_113 (
    .LSB(dda_111_msb_2), .in_2(dda_114_lsb_2), .in_3(dda_114_out_6), .MSB(dda_114_out_7),
    .LSB_2(dda_113_lsb_2), .out_6(dda_113_out_6), .out_7(dda_113_out_7), .MSB_2(dda_113_msb_2));
  DDA dda_114 (
    .LSB(dda_94_msb_2), .in_2(dda_96_lsb_2), .in_3(dda_96_out_6), .MSB(dda_96_out_7), .LSB_2(dda_114_lsb_2),
    .out_6(dda_114_out_6), .out_7(dda_114_out_7), .MSB_2(dda_114_msb_2));
  DDA dda_115 (
    .LSB(dda_113_msb_2), .in_2(dda_116_lsb_2), .in_3(dda_116_out_6), .MSB(dda_116_out_7),
    .LSB_2(dda_115_lsb_2), .out_6(dda_115_out_6), .out_7(dda_115_out_7), .MSB_2(dda_115_msb_2));
  DDA dda_116 (
    .LSB(dda_114_msb_2), .in_2(dda_117_lsb_2), .in_3(dda_117_out_6), .MSB(dda_117_out_7),
    .LSB_2(dda_116_lsb_2), .out_6(dda_116_out_6), .out_7(dda_116_out_7), .MSB_2(dda_116_msb_2));
  DDA dda_117 (
    .LSB(dda_96_msb_2), .in_2(dda_98_lsb_2), .in_3(dda_98_out_6), .MSB(dda_98_out_7), .LSB_2(dda_117_lsb_2),
    .out_6(dda_117_out_6), .out_7(dda_117_out_7), .MSB_2(dda_117_msb_2));
  DDA dda_118 (
    .LSB(dda_116_msb_2), .in_2(dda_119_lsb_2), .in_3(dda_119_out_6), .MSB(dda_119_out_7),
    .LSB_2(dda_118_lsb_2), .out_6(dda_118_out_6), .out_7(dda_118_out_7), .MSB_2(dda_118_msb_2));
  DDA dda_119 (
    .LSB(dda_117_msb_2), .in_2(dda_120_lsb_2), .in_3(dda_120_out_6), .MSB(dda_120_out_7),
    .LSB_2(dda_119_lsb_2), .out_6(dda_119_out_6), .out_7(dda_119_out_7), .MSB_2(dda_119_msb_2));
  DDA dda_120 (
    .LSB(dda_98_msb_2), .in_2(dda_100_lsb_2), .in_3(dda_100_out_6), .MSB(dda_100_out_7),
    .LSB_2(dda_120_lsb_2), .out_6(dda_120_out_6), .out_7(dda_120_out_7), .MSB_2(dda_120_msb_2));
  DDA dda_121 (
    .LSB(dda_119_msb_2), .in_2(dda_122_lsb_2), .in_3(dda_122_out_6), .MSB(dda_122_out_7),
    .LSB_2(dda_121_lsb_2), .out_6(dda_121_out_6), .out_7(dda_121_out_7), .MSB_2(dda_121_msb_2));
  DDA dda_122 (
    .LSB(dda_120_msb_2), .in_2(dda_123_lsb_2), .in_3(dda_123_out_6), .MSB(dda_123_out_7),
    .LSB_2(dda_122_lsb_2), .out_6(dda_122_out_6), .out_7(dda_122_out_7), .MSB_2(dda_122_msb_2));
  DDA dda_123 (
    .LSB(dda_100_msb_2), .in_2(dda_102_lsb_2), .in_3(dda_102_out_6), .MSB(dda_102_out_7),
    .LSB_2(dda_123_lsb_2), .out_6(dda_123_out_6), .out_7(dda_123_out_7), .MSB_2(dda_123_msb_2));
  DDA dda_124 (
    .LSB(dda_122_msb_2), .in_2(dda_125_lsb_2), .in_3(dda_125_out_6), .MSB(dda_125_out_7),
    .LSB_2(dda_124_lsb_2), .out_6(dda_124_out_6), .out_7(dda_124_out_7), .MSB_2(dda_124_msb_2));
  DDA dda_125 (
    .LSB(dda_123_msb_2), .in_2(dda_126_lsb_2), .in_3(dda_126_out_6), .MSB(dda_126_out_7),
    .LSB_2(dda_125_lsb_2), .out_6(dda_125_out_6), .out_7(dda_125_out_7), .MSB_2(dda_125_msb_2));
  DDA dda_126 (
    .LSB(dda_102_msb_2), .in_2(dda_104_lsb_2), .in_3(dda_104_out_6), .MSB(dda_104_out_7),
    .LSB_2(dda_126_lsb_2), .out_6(dda_126_out_6), .out_7(dda_126_out_7), .MSB_2(dda_126_msb_2));
  DDA dda_127 (
    .LSB(dda_125_msb_2), .in_2(dda_128_lsb_2), .in_3(dda_128_out_6), .MSB(dda_128_out_7),
    .LSB_2(dda_127_lsb_2), .out_6(dda_127_out_6), .out_7(dda_127_out_7), .MSB_2(dda_127_msb_2));
  DDA dda_128 (
    .LSB(dda_126_msb_2), .in_2(dda_104_msb_2), .in_3(dda_105_msb_2), .MSB(dda_91_msb_2),
    .LSB_2(dda_128_lsb_2), .out_6(dda_128_out_6), .out_7(dda_128_out_7), .MSB_2(dda_128_msb_2));
  DDA dda_129 (
    .LSB(register_1_q[4]), .in_2(dda_130_lsb_2), .in_3(dda_130_out_6), .MSB(dda_130_out_7),
    .LSB_2(dda_129_lsb_2), .out_6(dda_129_out_6), .out_7(dda_129_out_7), .MSB_2(dda_129_msb_2));
  DDA dda_130 (
    .LSB(register_1_q[5]), .in_2(dda_131_lsb_2), .in_3(dda_131_out_6), .MSB(dda_131_out_7),
    .LSB_2(dda_130_lsb_2), .out_6(dda_130_out_6), .out_7(dda_130_out_7), .MSB_2(dda_130_msb_2));
  DDA dda_131 (
    .LSB(register_1_q[6]), .in_2(dda_106_lsb_2), .in_3(dda_106_out_6), .MSB(dda_106_out_7),
    .LSB_2(dda_131_lsb_2), .out_6(dda_131_out_6), .out_7(dda_131_out_7), .MSB_2(dda_131_msb_2));
  DDA dda_132 (
    .LSB(dda_130_msb_2), .in_2(dda_133_lsb_2), .in_3(dda_133_out_6), .MSB(dda_133_out_7),
    .LSB_2(dda_132_lsb_2), .out_6(dda_132_out_6), .out_7(dda_132_out_7), .MSB_2(dda_132_msb_2));
  DDA dda_133 (
    .LSB(dda_131_msb_2), .in_2(dda_134_lsb_2), .in_3(dda_134_out_6), .MSB(dda_134_out_7),
    .LSB_2(dda_133_lsb_2), .out_6(dda_133_out_6), .out_7(dda_133_out_7), .MSB_2(dda_133_msb_2));
  DDA dda_134 (
    .LSB(dda_106_msb_2), .in_2(dda_109_lsb_2), .in_3(dda_109_out_6), .MSB(dda_109_out_7),
    .LSB_2(dda_134_lsb_2), .out_6(dda_134_out_6), .out_7(dda_134_out_7), .MSB_2(dda_134_msb_2));
  DDA dda_135 (
    .LSB(dda_133_msb_2), .in_2(dda_136_lsb_2), .in_3(dda_136_out_6), .MSB(dda_136_out_7),
    .LSB_2(dda_135_lsb_2), .out_6(dda_135_out_6), .out_7(dda_135_out_7), .MSB_2(dda_135_msb_2));
  DDA dda_136 (
    .LSB(dda_134_msb_2), .in_2(dda_137_lsb_2), .in_3(dda_137_out_6), .MSB(dda_137_out_7),
    .LSB_2(dda_136_lsb_2), .out_6(dda_136_out_6), .out_7(dda_136_out_7), .MSB_2(dda_136_msb_2));
  DDA dda_137 (
    .LSB(dda_109_msb_2), .in_2(dda_112_lsb_2), .in_3(dda_112_out_6), .MSB(dda_112_out_7),
    .LSB_2(dda_137_lsb_2), .out_6(dda_137_out_6), .out_7(dda_137_out_7), .MSB_2(dda_137_msb_2));
  DDA dda_138 (
    .LSB(dda_136_msb_2), .in_2(dda_139_lsb_2), .in_3(dda_139_out_6), .MSB(dda_139_out_7),
    .LSB_2(dda_138_lsb_2), .out_6(dda_138_out_6), .out_7(dda_138_out_7), .MSB_2(dda_138_msb_2));
  DDA dda_139 (
    .LSB(dda_137_msb_2), .in_2(dda_140_lsb_2), .in_3(dda_140_out_6), .MSB(dda_140_out_7),
    .LSB_2(dda_139_lsb_2), .out_6(dda_139_out_6), .out_7(dda_139_out_7), .MSB_2(dda_139_msb_2));
  DDA dda_140 (
    .LSB(dda_112_msb_2), .in_2(dda_115_lsb_2), .in_3(dda_115_out_6), .MSB(dda_115_out_7),
    .LSB_2(dda_140_lsb_2), .out_6(dda_140_out_6), .out_7(dda_140_out_7), .MSB_2(dda_140_msb_2));
  DDA dda_141 (
    .LSB(dda_139_msb_2), .in_2(dda_142_lsb_2), .in_3(dda_142_out_6), .MSB(dda_142_out_7),
    .LSB_2(dda_141_lsb_2), .out_6(dda_141_out_6), .out_7(dda_141_out_7), .MSB_2(dda_141_msb_2));
  DDA dda_142 (
    .LSB(dda_140_msb_2), .in_2(dda_143_lsb_2), .in_3(dda_143_out_6), .MSB(dda_143_out_7),
    .LSB_2(dda_142_lsb_2), .out_6(dda_142_out_6), .out_7(dda_142_out_7), .MSB_2(dda_142_msb_2));
  DDA dda_143 (
    .LSB(dda_115_msb_2), .in_2(dda_118_lsb_2), .in_3(dda_118_out_6), .MSB(dda_118_out_7),
    .LSB_2(dda_143_lsb_2), .out_6(dda_143_out_6), .out_7(dda_143_out_7), .MSB_2(dda_143_msb_2));
  DDA dda_144 (
    .LSB(dda_142_msb_2), .in_2(dda_145_lsb_2), .in_3(dda_145_out_6), .MSB(dda_145_out_7),
    .LSB_2(dda_144_lsb_2), .out_6(dda_144_out_6), .out_7(dda_144_out_7), .MSB_2(dda_144_msb_2));
  DDA dda_145 (
    .LSB(dda_143_msb_2), .in_2(dda_146_lsb_2), .in_3(dda_146_out_6), .MSB(dda_146_out_7),
    .LSB_2(dda_145_lsb_2), .out_6(dda_145_out_6), .out_7(dda_145_out_7), .MSB_2(dda_145_msb_2));
  DDA dda_146 (
    .LSB(dda_118_msb_2), .in_2(dda_121_lsb_2), .in_3(dda_121_out_6), .MSB(dda_121_out_7),
    .LSB_2(dda_146_lsb_2), .out_6(dda_146_out_6), .out_7(dda_146_out_7), .MSB_2(dda_146_msb_2));
  DDA dda_147 (
    .LSB(dda_145_msb_2), .in_2(dda_148_lsb_2), .in_3(dda_148_out_6), .MSB(dda_148_out_7),
    .LSB_2(dda_147_lsb_2), .out_6(dda_147_out_6), .out_7(dda_147_out_7), .MSB_2(dda_147_msb_2));
  DDA dda_148 (
    .LSB(dda_146_msb_2), .in_2(dda_149_lsb_2), .in_3(dda_149_out_6), .MSB(dda_149_out_7),
    .LSB_2(dda_148_lsb_2), .out_6(dda_148_out_6), .out_7(dda_148_out_7), .MSB_2(dda_148_msb_2));
  DDA dda_149 (
    .LSB(dda_121_msb_2), .in_2(dda_124_lsb_2), .in_3(dda_124_out_6), .MSB(dda_124_out_7),
    .LSB_2(dda_149_lsb_2), .out_6(dda_149_out_6), .out_7(dda_149_out_7), .MSB_2(dda_149_msb_2));
  DDA dda_150 (
    .LSB(dda_148_msb_2), .in_2(dda_151_lsb_2), .in_3(dda_151_out_6), .MSB(dda_151_out_7),
    .LSB_2(dda_150_lsb_2), .out_6(dda_150_out_6), .out_7(dda_150_out_7), .MSB_2(dda_150_msb_2));
  DDA dda_151 (
    .LSB(dda_149_msb_2), .in_2(dda_152_lsb_2), .in_3(dda_152_out_6), .MSB(dda_152_out_7),
    .LSB_2(dda_151_lsb_2), .out_6(dda_151_out_6), .out_7(dda_151_out_7), .MSB_2(dda_151_msb_2));
  DDA dda_152 (
    .LSB(dda_124_msb_2), .in_2(dda_127_lsb_2), .in_3(dda_127_out_6), .MSB(dda_127_out_7),
    .LSB_2(dda_152_lsb_2), .out_6(dda_152_out_6), .out_7(dda_152_out_7), .MSB_2(dda_152_msb_2));
  DDA dda_153 (
    .LSB(dda_151_msb_2), .in_2(dda_152_msb_2), .in_3(dda_127_msb_2), .MSB(dda_128_msb_2),
    .LSB_2(dda_153_lsb_2), .out_6(dda_153_out_6), .out_7(dda_153_out_7), .MSB_2(dda_180_msb_2[3]));
  _7seg_logic_encoder u_7seg_logic_encoder_1 (
    .Input(dda_180_msb_2), .A(out_40), .B(out_9), .C(out_39), .D(out_8), .E(out_38), .F(out_37), .G(out_7));
  DDA dda_154 (
    .LSB(register_1_q[2]), .in_2(dda_155_lsb_2), .in_3(dda_155_out_6), .MSB(dda_155_out_7),
    .LSB_2(dda_154_lsb_2), .out_6(dda_154_out_6), .out_7(dda_154_out_7), .MSB_2(dda_154_msb_2));
  DDA dda_155 (
    .LSB(register_1_q[3]), .in_2(dda_129_lsb_2), .in_3(dda_129_out_6), .MSB(dda_129_out_7),
    .LSB_2(dda_155_lsb_2), .out_6(dda_155_out_6), .out_7(dda_155_out_7), .MSB_2(dda_155_msb_2));
  DDA dda_156 (
    .LSB(dda_155_msb_2), .in_2(dda_157_lsb_2), .in_3(dda_157_out_6), .MSB(dda_157_out_7),
    .LSB_2(dda_156_lsb_2), .out_6(dda_156_out_6), .out_7(dda_156_out_7), .MSB_2(dda_156_msb_2));
  DDA dda_157 (
    .LSB(dda_129_msb_2), .in_2(dda_132_lsb_2), .in_3(dda_132_out_6), .MSB(dda_132_out_7),
    .LSB_2(dda_157_lsb_2), .out_6(dda_157_out_6), .out_7(dda_157_out_7), .MSB_2(dda_157_msb_2));
  DDA dda_158 (
    .LSB(dda_157_msb_2), .in_2(dda_159_lsb_2), .in_3(dda_159_out_6), .MSB(dda_159_out_7),
    .LSB_2(dda_158_lsb_2), .out_6(dda_158_out_6), .out_7(dda_158_out_7), .MSB_2(dda_158_msb_2));
  DDA dda_159 (
    .LSB(dda_132_msb_2), .in_2(dda_135_lsb_2), .in_3(dda_135_out_6), .MSB(dda_135_out_7),
    .LSB_2(dda_159_lsb_2), .out_6(dda_159_out_6), .out_7(dda_159_out_7), .MSB_2(dda_159_msb_2));
  DDA dda_160 (
    .LSB(dda_159_msb_2), .in_2(dda_161_lsb_2), .in_3(dda_161_out_6), .MSB(dda_161_out_7),
    .LSB_2(dda_160_lsb_2), .out_6(dda_160_out_6), .out_7(dda_160_out_7), .MSB_2(dda_160_msb_2));
  DDA dda_161 (
    .LSB(dda_135_msb_2), .in_2(dda_138_lsb_2), .in_3(dda_138_out_6), .MSB(dda_138_out_7),
    .LSB_2(dda_161_lsb_2), .out_6(dda_161_out_6), .out_7(dda_161_out_7), .MSB_2(dda_161_msb_2));
  DDA dda_162 (
    .LSB(dda_161_msb_2), .in_2(dda_163_lsb_2), .in_3(dda_163_out_6), .MSB(dda_163_out_7),
    .LSB_2(dda_162_lsb_2), .out_6(dda_162_out_6), .out_7(dda_162_out_7), .MSB_2(dda_162_msb_2));
  DDA dda_163 (
    .LSB(dda_138_msb_2), .in_2(dda_141_lsb_2), .in_3(dda_141_out_6), .MSB(dda_141_out_7),
    .LSB_2(dda_163_lsb_2), .out_6(dda_163_out_6), .out_7(dda_163_out_7), .MSB_2(dda_163_msb_2));
  DDA dda_164 (
    .LSB(dda_163_msb_2), .in_2(dda_165_lsb_2), .in_3(dda_165_out_6), .MSB(dda_165_out_7),
    .LSB_2(dda_164_lsb_2), .out_6(dda_164_out_6), .out_7(dda_164_out_7), .MSB_2(dda_164_msb_2));
  DDA dda_165 (
    .LSB(dda_141_msb_2), .in_2(dda_144_lsb_2), .in_3(dda_144_out_6), .MSB(dda_144_out_7),
    .LSB_2(dda_165_lsb_2), .out_6(dda_165_out_6), .out_7(dda_165_out_7), .MSB_2(dda_165_msb_2));
  DDA dda_166 (
    .LSB(dda_165_msb_2), .in_2(dda_167_lsb_2), .in_3(dda_167_out_6), .MSB(dda_167_out_7),
    .LSB_2(dda_166_lsb_2), .out_6(dda_166_out_6), .out_7(dda_166_out_7), .MSB_2(dda_166_msb_2));
  DDA dda_167 (
    .LSB(dda_144_msb_2), .in_2(dda_147_lsb_2), .in_3(dda_147_out_6), .MSB(dda_147_out_7),
    .LSB_2(dda_167_lsb_2), .out_6(dda_167_out_6), .out_7(dda_167_out_7), .MSB_2(dda_167_msb_2));
  DDA dda_168 (
    .LSB(dda_167_msb_2), .in_2(dda_169_lsb_2), .in_3(dda_169_out_6), .MSB(dda_169_out_7),
    .LSB_2(dda_168_lsb_2), .out_6(dda_168_out_6), .out_7(dda_168_out_7), .MSB_2(dda_168_msb_2));
  DDA dda_169 (
    .LSB(dda_147_msb_2), .in_2(dda_150_lsb_2), .in_3(dda_150_out_6), .MSB(dda_150_out_7),
    .LSB_2(dda_169_lsb_2), .out_6(dda_169_out_6), .out_7(dda_169_out_7), .MSB_2(dda_169_msb_2));
  DDA dda_170 (
    .LSB(dda_169_msb_2), .in_2(dda_171_lsb_2), .in_3(dda_171_out_6), .MSB(dda_171_out_7),
    .LSB_2(dda_170_lsb_2), .out_6(dda_170_out_6), .out_7(dda_170_out_7), .MSB_2(dda_180_msb_2[1]));
  DDA dda_171 (
    .LSB(dda_150_msb_2), .in_2(dda_153_lsb_2), .in_3(dda_153_out_6), .MSB(dda_153_out_7),
    .LSB_2(dda_171_lsb_2), .out_6(dda_171_out_6), .out_7(dda_171_out_7), .MSB_2(dda_180_msb_2[2]));
  DDA dda_172 (
    .LSB(register_1_q[1]), .in_2(dda_154_lsb_2), .in_3(dda_154_out_6), .MSB(dda_154_out_7),
    .LSB_2(register_1_q_2[1]), .out_6(register_1_q_2[2]), .out_7(register_1_q_2[3]), .MSB_2(dda_172_msb_2[0]));
  DDA dda_173 (
    .LSB(dda_154_msb_2), .in_2(dda_156_lsb_2), .in_3(dda_156_out_6), .MSB(dda_156_out_7),
    .LSB_2(dda_172_msb_2[1]), .out_6(dda_172_msb_2[2]), .out_7(dda_172_msb_2[3]), .MSB_2(dda_173_msb_2[0]));
  DDA dda_174 (
    .LSB(dda_156_msb_2), .in_2(dda_158_lsb_2), .in_3(dda_158_out_6), .MSB(dda_158_out_7),
    .LSB_2(dda_173_msb_2[1]), .out_6(dda_173_msb_2[2]), .out_7(dda_173_msb_2[3]), .MSB_2(dda_174_msb_2[0]));
  DDA dda_175 (
    .LSB(dda_158_msb_2), .in_2(dda_160_lsb_2), .in_3(dda_160_out_6), .MSB(dda_160_out_7),
    .LSB_2(dda_174_msb_2[1]), .out_6(dda_174_msb_2[2]), .out_7(dda_174_msb_2[3]), .MSB_2(dda_175_msb_2[0]));
  DDA dda_176 (
    .LSB(dda_160_msb_2), .in_2(dda_162_lsb_2), .in_3(dda_162_out_6), .MSB(dda_162_out_7),
    .LSB_2(dda_175_msb_2[1]), .out_6(dda_175_msb_2[2]), .out_7(dda_175_msb_2[3]), .MSB_2(dda_176_msb_2[0]));
  DDA dda_177 (
    .LSB(dda_162_msb_2), .in_2(dda_164_lsb_2), .in_3(dda_164_out_6), .MSB(dda_164_out_7),
    .LSB_2(dda_176_msb_2[1]), .out_6(dda_176_msb_2[2]), .out_7(dda_176_msb_2[3]), .MSB_2(dda_177_msb_2[0]));
  DDA dda_178 (
    .LSB(dda_164_msb_2), .in_2(dda_166_lsb_2), .in_3(dda_166_out_6), .MSB(dda_166_out_7),
    .LSB_2(dda_177_msb_2[1]), .out_6(dda_177_msb_2[2]), .out_7(dda_177_msb_2[3]), .MSB_2(dda_178_msb_2[0]));
  DDA dda_179 (
    .LSB(dda_166_msb_2), .in_2(dda_168_lsb_2), .in_3(dda_168_out_6), .MSB(dda_168_out_7),
    .LSB_2(dda_178_msb_2[1]), .out_6(dda_178_msb_2[2]), .out_7(dda_178_msb_2[3]), .MSB_2(dda_179_msb_2[0]));
  DDA dda_180 (
    .LSB(dda_168_msb_2), .in_2(dda_170_lsb_2), .in_3(dda_170_out_6), .MSB(dda_170_out_7),
    .LSB_2(dda_179_msb_2[1]), .out_6(dda_179_msb_2[2]), .out_7(dda_179_msb_2[3]), .MSB_2(dda_180_msb_2[0]));
  _7seg_logic_encoder u_7seg_logic_encoder_2 (
    .Input(dda_179_msb_2), .A(out_44), .B(out_12), .C(out_43), .D(out_11), .E(out_42), .F(out_41), .G(out_10));
  _7seg_logic_encoder u_7seg_logic_encoder_3 (
    .Input(dda_178_msb_2), .A(out_48), .B(out_15), .C(out_47), .D(out_14), .E(out_46), .F(out_45), .G(out_13));
  _7seg_logic_encoder u_7seg_logic_encoder_4 (
    .Input(dda_177_msb_2), .A(out_52), .B(out_18), .C(out_51), .D(out_17), .E(out_50), .F(out_49), .G(out_16));
  _7seg_logic_encoder u_7seg_logic_encoder_5 (
    .Input(dda_176_msb_2), .A(out_56), .B(out_21), .C(out_55), .D(out_20), .E(out_54), .F(out_53), .G(out_19));
  _7seg_logic_encoder u_7seg_logic_encoder_6 (
    .Input(dda_175_msb_2), .A(out_60), .B(out_24), .C(out_59), .D(out_23), .E(out_58), .F(out_57), .G(out_22));
  _7seg_logic_encoder u_7seg_logic_encoder_7 (
    .Input(dda_174_msb_2), .A(out_64), .B(out_27), .C(out_63), .D(out_26), .E(out_62), .F(out_61), .G(out_25));
  _7seg_logic_encoder u_7seg_logic_encoder_8 (
    .Input(dda_173_msb_2), .A(out_68), .B(out_30), .C(out_67), .D(out_29), .E(out_66), .F(out_65), .G(out_28));
  _7seg_logic_encoder u_7seg_logic_encoder_9 (
    .Input(dda_172_msb_2), .A(out_72), .B(out_33), .C(out_71), .D(out_32), .E(out_70), .F(out_69), .G(out_31));
  _7seg_logic_encoder u_7seg_logic_encoder_10 (
    .Input(register_1_q_2), .A(_1), .B(_2), .C(_3), .D(_4), .E(_5), .F(_7), .G(_6));
endmodule

module _7seg_logic_encoder (
  input  [3:0] Input,
  output A,
  output B,
  output C,
  output D,
  output E,
  output F,
  output G
);

  wire decoder_1_out0, decoder_1_out1, decoder_1_out2, decoder_1_out3, decoder_1_out4, decoder_1_out5,
       decoder_1_out6, decoder_1_out7, decoder_1_out8, decoder_1_out9;

  Decoder #(.select(4), .enable("false")) decoder_1 (
    .out0(decoder_1_out0), .out1(decoder_1_out1), .out2(decoder_1_out2), .out3(decoder_1_out3),
    .out4(decoder_1_out4), .out5(decoder_1_out5), .out6(decoder_1_out6), .out7(decoder_1_out7),
    .out8(decoder_1_out8), .out9(decoder_1_out9), .sel(Input));  // open: out10, out11, out12, out13, out14, out15
  or u_A (A, decoder_1_out0, decoder_1_out2, decoder_1_out3, decoder_1_out5, decoder_1_out6, decoder_1_out7, decoder_1_out8, decoder_1_out9);
  or u_B (B, decoder_1_out0, decoder_1_out1, decoder_1_out2, decoder_1_out3, decoder_1_out4, decoder_1_out7, decoder_1_out8, decoder_1_out9);
  or u_C (C, decoder_1_out0, decoder_1_out1, decoder_1_out3, decoder_1_out4, decoder_1_out5, decoder_1_out6, decoder_1_out7, decoder_1_out8, decoder_1_out9);
  or u_D (D, decoder_1_out0, decoder_1_out2, decoder_1_out3, decoder_1_out5, decoder_1_out6, decoder_1_out8);
  or u_E (E, decoder_1_out0, decoder_1_out2, decoder_1_out6, decoder_1_out8);
  or u_F (F, decoder_1_out0, decoder_1_out4, decoder_1_out5, decoder_1_out6, decoder_1_out7, decoder_1_out8, decoder_1_out9);
  or u_G (G, decoder_1_out2, decoder_1_out3, decoder_1_out4, decoder_1_out5, decoder_1_out6, decoder_1_out8, decoder_1_out9);
endmodule

module DDA (
  input  LSB,
  input  in_2,
  input  in_3,
  input  MSB,
  output LSB_2,
  output out_6,
  output out_7,
  output MSB_2
);

  wire decoder_1_out0, decoder_1_out1, decoder_1_out2, decoder_1_out3, decoder_1_out4, decoder_1_out5,
       decoder_1_out6, decoder_1_out7, decoder_1_out8, decoder_1_out9, nor_1_out, or_1_out, or_2_out;
  wire [3:0] adder_1_out, multiplexer_1_out, pull_resistor_2_node;
  wire [3:3] pull_resistor_1_node;

  Pull_Resistor pull_resistor_1 (.node(pull_resistor_1_node[3]));
  or or_1 (or_1_out, decoder_1_out0, decoder_1_out1, decoder_1_out2, decoder_1_out3, decoder_1_out4);
  Decoder #(.select(4), .disabled(0), .enable("false")) decoder_1 (
    .out0(decoder_1_out0), .out1(decoder_1_out1), .out2(decoder_1_out2), .out3(decoder_1_out3),
    .out4(decoder_1_out4), .out5(decoder_1_out5), .out6(decoder_1_out6), .out7(decoder_1_out7),
    .out8(decoder_1_out8), .out9(decoder_1_out9), .sel({MSB, in_3, in_2, LSB}));  // open: out10, out11, out12, out13, out14, out15
  nor nor_1 (nor_1_out, or_2_out, or_1_out);
  Multiplexer #(.width(4)) multiplexer_1 (
    .in0({MSB, in_3, in_2, LSB}), .in1(adder_1_out), .out(multiplexer_1_out), .sel(or_2_out));  // open: en
  Adder #(.width(4)) adder_1 (
    .a({MSB, in_3, in_2, LSB}), .b({{2{pull_resistor_1_node[3]}}, 2'b11}), .out(adder_1_out));  // open: cin, cout
  Pull_Resistor pull_resistor_2 (.node(pull_resistor_2_node));
  or or_2 (or_2_out, decoder_1_out5, decoder_1_out6, decoder_1_out7, decoder_1_out8, decoder_1_out9);
  Multiplexer #(.width(4)) multiplexer_2 (
    .in0(multiplexer_1_out), .in1(pull_resistor_2_node), .out({MSB_2, out_7, out_6, LSB_2}), .sel(nor_1_out));  // open: en
endmodule
