// Logisim project RegisterFile.circ as structural Verilog: 1 circuit, main circuit Register_File
module Register_File (
  input  [4:0] RD,
  input  [4:0] RS1_in,
  input  read_en,
  input  [4:0] RS2_in,
  input  [31:0] ALU_in,
  input  Dmem_rd,
  input  [31:0] Dmem_in,
  input  Clock,
  input  RegWriteEnable,
  input  Reset,
  output [31:0] RS1_out,
  output [31:0] RS2_out
);

  wire and_1_out, and_2_out, and_3_out, and_4_out, and_5_out, and_6_out, and_7_out, and_8_out, and_9_out,
       and_10_out, and_11_out, and_12_out, and_13_out, and_14_out, and_15_out, and_16_out, and_17_out,
       and_18_out, and_19_out, and_20_out, and_21_out, and_22_out, and_23_out, and_24_out, and_25_out,
       and_26_out, and_27_out, and_28_out, and_29_out, and_30_out, and_31_out, and_32_out, d_ff_1_q,
       d_ff_1_qn, decoder_1_out0, decoder_1_out1, decoder_1_out2, decoder_1_out3, decoder_1_out4,
       decoder_1_out5, decoder_1_out6, decoder_1_out7, decoder_1_out8, decoder_1_out9, decoder_1_out10,
       decoder_1_out11, decoder_1_out12, decoder_1_out13, decoder_1_out14, decoder_1_out15, decoder_1_out16,
       decoder_1_out17, decoder_1_out18, decoder_1_out19, decoder_1_out20, decoder_1_out21, decoder_1_out22,
       decoder_1_out23, decoder_1_out24, decoder_1_out25, decoder_1_out26, decoder_1_out27, decoder_1_out28,
       decoder_1_out29, decoder_1_out30, decoder_1_out31;
  wire [31:0] multiplexer_1_out, multiplexer_2_out, multiplexer_3_out, register_1_q, register_2_q,
       register_3_q, register_4_q, register_5_q, register_6_q, register_7_q, register_8_q, register_9_q,
       register_10_q, register_11_q, register_12_q, register_13_q, register_14_q, register_15_q,
       register_16_q, register_17_q, register_18_q, register_19_q, register_20_q, register_21_q,
       register_22_q, register_23_q, register_24_q, register_25_q, register_26_q, register_27_q,
       register_28_q, register_29_q, register_30_q, register_31_q, register_32_q;

  Decoder #(.select(5)) decoder_1 (
    .out0(decoder_1_out0), .out1(decoder_1_out1), .out2(decoder_1_out2), .out3(decoder_1_out3),
    .out4(decoder_1_out4), .out5(decoder_1_out5), .out6(decoder_1_out6), .out7(decoder_1_out7),
    .out8(decoder_1_out8), .out9(decoder_1_out9), .out10(decoder_1_out10), .out11(decoder_1_out11),
    .out12(decoder_1_out12), .out13(decoder_1_out13), .out14(decoder_1_out14), .out15(decoder_1_out15),
    .out16(decoder_1_out16), .out17(decoder_1_out17), .out18(decoder_1_out18), .out19(decoder_1_out19),
    .out20(decoder_1_out20), .out21(decoder_1_out21), .out22(decoder_1_out22), .out23(decoder_1_out23),
    .out24(decoder_1_out24), .out25(decoder_1_out25), .out26(decoder_1_out26), .out27(decoder_1_out27),
    .out28(decoder_1_out28), .out29(decoder_1_out29), .out30(decoder_1_out30), .out31(decoder_1_out31),
    .sel(RD));  // open: en
  Multiplexer #(.width(32)) multiplexer_1 (
    .in0(ALU_in), .in1(Dmem_in), .out(multiplexer_1_out), .sel(Dmem_rd));  // open: en
  and and_1 (and_1_out, decoder_1_out0, RegWriteEnable);
  and and_2 (and_2_out, decoder_1_out2, RegWriteEnable);
  and and_3 (and_3_out, decoder_1_out4, RegWriteEnable);
  and and_4 (and_4_out, decoder_1_out6, RegWriteEnable);
  and and_5 (and_5_out, decoder_1_out8, RegWriteEnable);
  and and_6 (and_6_out, decoder_1_out10, RegWriteEnable);
  and and_7 (and_7_out, decoder_1_out12, RegWriteEnable);
  and and_8 (and_8_out, decoder_1_out14, RegWriteEnable);
  and and_9 (and_9_out, RegWriteEnable, decoder_1_out16);
  and and_10 (and_10_out, RegWriteEnable, decoder_1_out18);
  and and_11 (and_11_out, RegWriteEnable, decoder_1_out20);
  and and_12 (and_12_out, RegWriteEnable, decoder_1_out22);
  and and_13 (and_13_out, RegWriteEnable, decoder_1_out24);
  and and_14 (and_14_out, RegWriteEnable, decoder_1_out26);
  and and_15 (and_15_out, RegWriteEnable, decoder_1_out28);
  and and_16 (and_16_out, RegWriteEnable, decoder_1_out30);
  Register #(.width(32)) register_1 (.en(and_1_out), .Q(register_1_q), .clk(d_ff_1_q), .clr(Reset));  // open: D
  Register #(.width(32)) register_2 (
    .D(multiplexer_1_out), .en(and_2_out), .Q(register_2_q), .clk(d_ff_1_q), .clr(Reset));
  Register #(.width(32)) register_3 (
    .D(multiplexer_1_out), .en(and_3_out), .Q(register_3_q), .clk(d_ff_1_q), .clr(Reset));
  Register #(.width(32)) register_4 (
    .D(multiplexer_1_out), .en(and_4_out), .Q(register_4_q), .clk(d_ff_1_q), .clr(Reset));
  Register #(.width(32)) register_5 (
    .D(multiplexer_1_out), .en(and_5_out), .Q(register_5_q), .clk(d_ff_1_q), .clr(Reset));
  Register #(.width(32)) register_6 (
    .D(multiplexer_1_out), .en(and_6_out), .Q(register_6_q), .clk(d_ff_1_q), .clr(Reset));
  Register #(.width(32)) register_7 (
    .D(multiplexer_1_out), .en(and_7_out), .Q(register_7_q), .clk(d_ff_1_q), .clr(Reset));
  Register #(.width(32)) register_8 (
    .D(multiplexer_1_out), .en(and_8_out), .Q(register_8_q), .clk(d_ff_1_q), .clr(Reset));
  Register #(.width(32)) register_9 (
    .D(multiplexer_1_out), .en(and_9_out), .Q(register_9_q), .clk(d_ff_1_q), .clr(Reset));
  Register #(.width(32)) register_10 (
    .D(multiplexer_1_out), .en(and_10_out), .Q(register_10_q), .clk(d_ff_1_q), .clr(Reset));
  Register #(.width(32)) register_11 (
    .D(multiplexer_1_out), .en(and_11_out), .Q(register_11_q), .clk(d_ff_1_q), .clr(Reset));
  Register #(.width(32)) register_12 (
    .D(multiplexer_1_out), .en(and_12_out), .Q(register_12_q), .clk(d_ff_1_q), .clr(Reset));
  Register #(.width(32)) register_13 (
    .D(multiplexer_1_out), .en(and_13_out), .Q(register_13_q), .clk(d_ff_1_q), .clr(Reset));
  Register #(.width(32)) register_14 (
    .D(multiplexer_1_out), .en(and_14_out), .Q(register_14_q), .clk(d_ff_1_q), .clr(Reset));
  Register #(.width(32)) register_15 (
    .D(multiplexer_1_out), .en(and_15_out), .Q(register_15_q), .clk(d_ff_1_q), .clr(Reset));
  Register #(.width(32)) register_16 (
    .D(multiplexer_1_out), .en(and_16_out), .Q(register_16_q), .clk(d_ff_1_q), .clr(Reset));
  D_Flip_Flop d_ff_1 (.clk(Clock), .D(d_ff_1_qn), .Q(d_ff_1_q), .Qn(d_ff_1_qn), .preset(Reset));  // open: en, reset
  Register #(.width(32)) register_17 (
    .D(multiplexer_1_out), .en(and_17_out), .Q(register_17_q), .clk(d_ff_1_q), .clr(Reset));
  and and_17 (and_17_out, decoder_1_out1, RegWriteEnable);
  Register #(.width(32)) register_18 (
    .D(multiplexer_1_out), .en(and_18_out), .Q(register_18_q), .clk(d_ff_1_q), .clr(Reset));
  and and_18 (and_18_out, decoder_1_out3, RegWriteEnable);
  Register #(.width(32)) register_19 (
    .D(multiplexer_1_out), .en(and_19_out), .Q(register_19_q), .clk(d_ff_1_q), .clr(Reset));
  and and_19 (and_19_out, decoder_1_out5, RegWriteEnable);
  Register #(.width(32)) register_20 (
    .D(multiplexer_1_out), .en(and_20_out), .Q(register_20_q), .clk(d_ff_1_q), .clr(Reset));
  and and_20 (and_20_out, decoder_1_out7, RegWriteEnable);
  Register #(.width(32)) register_21 (
    .D(multiplexer_1_out), .en(and_21_out), .Q(register_21_q), .clk(d_ff_1_q), .clr(Reset));
  and and_21 (and_21_out, decoder_1_out9, RegWriteEnable);
  Register #(.width(32)) register_22 (
    .D(multiplexer_1_out), .en(and_22_out), .Q(register_22_q), .clk(d_ff_1_q), .clr(Reset));
  and and_22 (and_22_out, decoder_1_out11, RegWriteEnable);
  Register #(.width(32)) register_23 (
    .D(multiplexer_1_out), .en(and_23_out), .Q(register_23_q), .clk(d_ff_1_q), .clr(Reset));
  and and_23 (and_23_out, decoder_1_out13, RegWriteEnable);
  Register #(.width(32)) register_24 (
    .D(multiplexer_1_out), .en(and_24_out), .Q(register_24_q), .clk(d_ff_1_q), .clr(Reset));
  and and_24 (and_24_out, decoder_1_out15, RegWriteEnable);
  Register #(.width(32)) register_25 (
    .D(multiplexer_1_out), .en(and_25_out), .Q(register_25_q), .clk(d_ff_1_q), .clr(Reset));
  and and_25 (and_25_out, RegWriteEnable, decoder_1_out17);
  Register #(.width(32)) register_26 (
    .D(multiplexer_1_out), .en(and_26_out), .Q(register_26_q), .clk(d_ff_1_q), .clr(Reset));
  and and_26 (and_26_out, RegWriteEnable, decoder_1_out19);
  Register #(.width(32)) register_27 (
    .D(multiplexer_1_out), .en(and_27_out), .Q(register_27_q), .clk(d_ff_1_q), .clr(Reset));
  and and_27 (and_27_out, RegWriteEnable, decoder_1_out21);
  Register #(.width(32)) register_28 (
    .D(multiplexer_1_out), .en(and_28_out), .Q(register_28_q), .clk(d_ff_1_q), .clr(Reset));
  and and_28 (and_28_out, RegWriteEnable, decoder_1_out23);
  Register #(.width(32)) register_29 (
    .D(multiplexer_1_out), .en(and_29_out), .Q(register_29_q), .clk(d_ff_1_q), .clr(Reset));
  and and_29 (and_29_out, RegWriteEnable, decoder_1_out25);
  Register #(.width(32)) register_30 (
    .D(multiplexer_1_out), .en(and_30_out), .Q(register_30_q), .clk(d_ff_1_q), .clr(Reset));
  and and_30 (and_30_out, RegWriteEnable, decoder_1_out27);
  Register #(.width(32)) register_31 (
    .D(multiplexer_1_out), .en(and_31_out), .Q(register_31_q), .clk(d_ff_1_q), .clr(Reset));
  and and_31 (and_31_out, RegWriteEnable, decoder_1_out29);
  Register #(.width(32)) register_32 (
    .D(multiplexer_1_out), .en(and_32_out), .Q(register_32_q), .clk(d_ff_1_q), .clr(Reset));
  and and_32 (and_32_out, RegWriteEnable, decoder_1_out31);
  Multiplexer #(.select(5), .width(32)) multiplexer_2 (
    .in0(register_1_q), .in1(register_17_q), .in2(register_2_q), .in3(register_18_q), .in4(register_3_q),
    .in5(register_19_q), .in6(register_4_q), .in7(register_20_q), .in8(register_5_q), .in9(register_21_q),
    .in10(register_6_q), .in11(register_22_q), .in12(register_7_q), .in13(register_23_q),
    .in14(register_8_q), .in15(register_24_q), .in16(register_25_q), .in17(register_9_q),
    .in18(register_26_q), .in19(register_10_q), .in20(register_27_q), .in21(register_11_q),
    .in22(register_28_q), .in23(register_12_q), .in24(register_29_q), .in25(register_13_q),
    .in26(register_30_q), .in27(register_14_q), .in28(register_31_q), .in29(register_15_q),
    .in30(register_32_q), .in31(register_16_q), .out(multiplexer_2_out), .sel(RS1_in));  // open: en
  Multiplexer #(.select(5), .width(32)) multiplexer_3 (
    .in0(register_1_q), .in1(register_17_q), .in2(register_2_q), .in3(register_18_q), .in4(register_3_q),
    .in5(register_19_q), .in6(register_4_q), .in7(register_20_q), .in8(register_5_q), .in9(register_21_q),
    .in10(register_6_q), .in11(register_22_q), .in12(register_7_q), .in13(register_23_q),
    .in14(register_8_q), .in15(register_24_q), .in16(register_25_q), .in17(register_9_q),
    .in18(register_26_q), .in19(register_10_q), .in20(register_27_q), .in21(register_11_q),
    .in22(register_28_q), .in23(register_12_q), .in24(register_29_q), .in25(register_13_q),
    .in26(register_30_q), .in27(register_14_q), .in28(register_31_q), .in29(register_15_q),
    .in30(register_32_q), .in31(register_16_q), .out(multiplexer_3_out), .sel(RS2_in));  // open: en
  Pull_Resistor pull_resistor_1 (.node(RS1_out));
  assign RS1_out = read_en ? multiplexer_2_out : 32'bz;  // Controlled_Buffer controlled_buffer_1
  Pull_Resistor pull_resistor_2 (.node(RS2_out));
  assign RS2_out = read_en ? multiplexer_3_out : 32'bz;  // Controlled_Buffer controlled_buffer_2
endmodule
